// Logisim project computer_v0.circ as structural Verilog: 25 circuits, main circuit Computer
module Computer (
  input  reset,
  input  in_2,
  input  [7:0] keyboard,
  input  in_4,
  input  in_5
);

  wire conditionunit_1_r, decoderunit_1_mode, dotmatrix_1_p1, dotmatrix_2_p1, registerbank_1_disout,
       registerbank_1_distick, serialise_8_1_serial, serialise_8_1_tick, timer_out;
  wire [2:0] decoderunit_1_adr;
  wire [3:0] alu_1_status, decoderunit_1_alu, decoderunit_1_con, decoderunit_1_sel;
  wire [7:0] alu_1_result, decoderunit_1_data, mux_16_to_8_1_r, registerbank_1_aout, registerbank_1_dout,
       registerbank_1_hiout, registerbank_1_loout, registerbank_1_pout, registerbank_1_ramout,
       registerbank_1_spout, registerselectunit_1_x, registerselectunit_1_y;
  wire [15:0] dotmatrix_1_p2, dotmatrix_1_p3, dotmatrix_2_p2, dotmatrix_2_p3, programcounter_1_adr,
       rom_1_data;

  Clock timer (.out(timer_out));
  ROM #(.addrWidth(16), .dataWidth(16)) rom_1 (.addr(programcounter_1_adr), .data(rom_1_data));
  ProgramCounter programcounter_1 (
    .reset(reset), .clock(timer_out), .jmp(conditionunit_1_r),
    .override({registerbank_1_hiout, registerbank_1_loout}), .adr(programcounter_1_adr));
  ALU_ic alu_ic_1 ();  // open: s, x, y, result, status
  serialise_8 serialise_8_1 (
    .data(keyboard), .tick(serialise_8_1_tick), .serial(serialise_8_1_serial));  // open: start, clock
  DecoderUnit decoderunit_1 (
    .opcode(rom_1_data), .data(decoderunit_1_data), .con(decoderunit_1_con), .adr(decoderunit_1_adr),
    .mode(decoderunit_1_mode), .sel(decoderunit_1_sel), .alu(decoderunit_1_alu));
  RegisterBank registerbank_1 (
    .adr(decoderunit_1_adr), .clock(timer_out), .reset(reset), .data(mux_16_to_8_1_r),
    .sINdata(serialise_8_1_serial), .sINclock(serialise_8_1_tick), .sync(in_2), .SPout(registerbank_1_spout),
    .Aout(registerbank_1_aout), .Dout(registerbank_1_dout), .LOout(registerbank_1_loout),
    .HIout(registerbank_1_hiout), .DISout(registerbank_1_disout), .DIStick(registerbank_1_distick),
    .RAMout(registerbank_1_ramout), .Pout(registerbank_1_pout));
  RegisterSelectUnit registerselectunit_1 (
    .s(decoderunit_1_sel), .A(registerbank_1_aout), .HI(registerbank_1_hiout), .LO(registerbank_1_loout),
    .P(registerbank_1_pout), .D(registerbank_1_dout), .RAM(registerbank_1_ramout), .SP(registerbank_1_spout),
    .x(registerselectunit_1_x), .y(registerselectunit_1_y));
  // DotMatrix #(.dotshape("circle"), .inputtype("select"), .matrixcols(16), .matrixrows(16)) dotmatrix_1: pin names not known; wires that end beside it: dotmatrix_1_p1, dotmatrix_1_p2, dotmatrix_1_p3
  MatrixController_16p matrixcontroller_16p_1 (
    .serial(registerbank_1_distick), .clock(registerbank_1_disout), .anode(dotmatrix_1_p2),
    .ll(dotmatrix_1_p1), .kathode(dotmatrix_1_p3));
  // DotMatrix #(.dotshape("circle"), .inputtype("select"), .matrixcols(16), .matrixrows(16)) dotmatrix_2: pin names not known; wires that end beside it: dotmatrix_2_p1, dotmatrix_2_p2, dotmatrix_2_p3
  MatrixController_16p matrixcontroller_16p_2 (
    .serial(in_4), .clock(in_5), .anode(dotmatrix_2_p2), .ll(dotmatrix_2_p1), .kathode(dotmatrix_2_p3));
  ALU alu_1 (
    .s(decoderunit_1_alu), .x(registerselectunit_1_x), .y(registerselectunit_1_y), .result(alu_1_result),
    .status(alu_1_status));
  ConditionUnit conditionunit_1 (.status(alu_1_status), .s(decoderunit_1_con), .r(conditionunit_1_r));
  mux_16_to_8 mux_16_to_8_1 (.d1(decoderunit_1_data), .d0(alu_1_result), .s(decoderunit_1_mode), .r(mux_16_to_8_1_r));

  // Notes on the sheet:
  //   contents of rom_1 (hex, n*v repeats v):
  //   0 9080 a0a5
endmodule

module ALU (
  input  [7:0] x,
  input  [7:0] y,
  input  [3:0] s,
  output [3:0] status,
  output [7:0] result
);

  wire adder_1_cout, controlled_inverter_3_out, is_negative_1_r, is_negative_2_r, is_negative_3_r, nor_1_out,
       nor_2_out, nor_3_out, nor_4_out, nor_5_out, nor_6_out, nor_7_out, nor_8_out, nor_9_out, nor_10_out,
       nor_12_out, nor_13_out, not_1_out, not_2_out, not_3_out, not_4_out, not_5_out, not_6_out, not_7_out,
       or_1_out, shift_left_8_1_v, shift_right_8_1_v, xor_1_out, xor_2_out;
  wire [7:0] adder_1_out, controlled_buffer_1_out, controlled_buffer_3_out, controlled_buffer_4_out,
       nand_1_out, nor_11_out, shift_left_8_1_r, shift_right_8_1_r, xor_3_out, zero_msb_8_1_r;

  not not_1 (not_1_out, s[3]);
  not not_2 (not_2_out, s[2]);
  not not_3 (not_3_out, s[1]);
  not not_4 (not_4_out, s[0]);
  nor nor_1 (nor_1_out, not_2_out, s[3]);
  nor nor_2 (nor_2_out, not_4_out, s[1], s[2], s[3]);
  nor nor_3 (nor_3_out, s[0], s[1], s[2], s[3]);
  nor nor_4 (nor_4_out, s[0], not_3_out, s[2]);
  nor nor_5 (nor_5_out, s[0], s[1], s[2], not_1_out);
  nor nor_6 (nor_6_out, not_4_out, s[1], s[2], not_1_out);
  nor nor_7 (nor_7_out, not_3_out, not_2_out, not_1_out);
  nor nor_8 (nor_8_out, s[0], s[1], not_2_out, not_1_out);
  nor nor_9 (nor_9_out, not_4_out, s[1], not_2_out, not_1_out);
  is_negative is_negative_1 (.a(x), .r(is_negative_1_r));
  is_negative is_negative_2 (.a(y), .r(is_negative_2_r));
  nor nor_10 (nor_10_out, s[1], nor_4_out);
  assign controlled_buffer_1_out = s[0] ? 8'h1 : 8'bz;  // Controlled_Buffer controlled_buffer_1
  assign controlled_buffer_1_out = not_4_out ? y : 8'bz;  // Controlled_Buffer controlled_buffer_2
  zero_msb_8 zero_msb_8_1 (.a(x), .r(zero_msb_8_1_r));
  is_negative is_negative_3 (.a(adder_1_out), .r(is_negative_3_r));
  shift_right_8 shift_right_8_1 (.a(x), .v(shift_right_8_1_v), .r(shift_right_8_1_r));
  shift_left_8 shift_left_8_1 (.a(x), .v(shift_left_8_1_v), .r(shift_left_8_1_r));
  assign controlled_buffer_3_out = not_4_out ? y : 8'bz;  // Controlled_Buffer controlled_buffer_3
  Pull_Resistor #(.pull(1)) pull_resistor_1 (.node(controlled_buffer_3_out));
  assign nand_1_out = ~(x & y);  // NAND_Gate nand_1, 8 bits wide
  assign result = nor_8_out ? ~nand_1_out : 8'bz;  // Controlled_Inverter controlled_inverter_1
  assign nor_11_out = ~(x | y);  // NOR_Gate nor_11, 8 bits wide
  assign result = nor_9_out ? ~nor_11_out : 8'bz;  // Controlled_Inverter controlled_inverter_2
  xor xor_1 (xor_1_out, is_negative_1_r, is_negative_2_r);
  not not_5 (not_5_out, nor_10_out);
  assign controlled_buffer_4_out = nor_10_out ? controlled_buffer_1_out : 8'bz;  // Controlled_Buffer controlled_buffer_4
  xor xor_2 (xor_2_out, is_negative_3_r, not_1_out);
  nor nor_12 (nor_12_out, xor_2_out, not_6_out);
  not not_6 (not_6_out, nor_4_out);
  assign controlled_inverter_3_out = nor_5_out ? ~shift_right_8_1_v : 1'bz;  // Controlled_Inverter controlled_inverter_3
  assign result = nor_5_out ? shift_right_8_1_r : 8'bz;  // Controlled_Buffer controlled_buffer_5
  assign result = nor_6_out ? shift_left_8_1_r : 8'bz;  // Controlled_Buffer controlled_buffer_6
  assign controlled_inverter_3_out = nor_6_out ? ~shift_left_8_1_v : 1'bz;  // Controlled_Inverter controlled_inverter_4
  assign xor_3_out = controlled_buffer_3_out ^ x;  // XOR_Gate xor_3, 8 bits wide
  assign result = nor_7_out ? xor_3_out : 8'bz;  // Controlled_Buffer controlled_buffer_7
  Adder adder_1 (.a(x), .b(controlled_buffer_4_out), .out(adder_1_out), .cin(not_5_out), .cout(adder_1_cout));
  assign controlled_buffer_4_out = not_5_out ? ~controlled_buffer_1_out : 8'bz;  // Controlled_Inverter controlled_inverter_5
  assign result = nor_2_out ? zero_msb_8_1_r : 8'bz;  // Controlled_Buffer controlled_buffer_8
  not not_7 (not_7_out, xor_2_out);
  nor nor_13 (nor_13_out, not_7_out, not_6_out);
  assign result = or_1_out ? x : 8'bz;  // Controlled_Buffer controlled_buffer_9
  assign result = nor_12_out ? y : 8'bz;  // Controlled_Buffer controlled_buffer_10
  and and_1 (status[3], adder_1_cout, xor_1_out);
  Pull_Resistor #(.pull(1)) pull_resistor_2 (.node(result));
  assign result = nor_1_out ? adder_1_out : 8'bz;  // Controlled_Buffer controlled_buffer_11
  or or_1 (or_1_out, nor_3_out, nor_13_out);
  assign controlled_inverter_3_out = nor_1_out ? ~adder_1_cout : 1'bz;  // Controlled_Inverter controlled_inverter_6
  Pull_Resistor #(.pull(1)) pull_resistor_3 (.node(controlled_inverter_3_out));
  is_negative is_negative_4 (.a(result), .r(status[0]));
  is_zero is_zero_1 (.a(result), .r(status[1]));
  not not_8 (status[2], controlled_inverter_3_out);

  // Notes on the sheet:
  //   difference
  //   Z zero
  //   N negative
  //   C carry out
  //   V overflow
endmodule

module ALU_ic (
  input  [3:0] s,
  input  [7:0] x,
  input  [7:0] y,
  output [7:0] result,
  output [3:0] status
);

  wire n7402_1_pin1, n7402_1_pin2, n7402_1_pin3, n7402_1_pin4, n7402_1_pin5, n7402_1_pin6, n7402_1_pin8,
       n7402_1_pin10, n7402_1_pin11, n7402_1_pin12, n7410_1_pin6, n7410_1_pin8, n7410_1_pin12, n7410_2_pin3,
       n7410_2_pin5, n7410_2_pin6, n7410_2_pin8, n7410_2_pin10, n7410_2_pin11, n7420_1_pin8, n7420_2_pin4,
       n7420_2_pin8, n7427_1_pin6, n7486_1_pin3, n7486_1_pin6, n7486_1_pin8, n7486_1_pin11, n7486_2_pin3,
       n7486_2_pin6, n7486_2_pin8, n7486_2_pin11, n7486_3_pin11, n74240_1_pin12, n74240_1_pin14,
       n74240_1_pin16, n74240_1_pin18, n74240_2_pin1, n74240_4_pin1, n74244_1_pin3, n74244_1_pin5,
       n74244_1_pin7, n74244_1_pin9, n74244_1_pin12, n74244_1_pin14, n74244_1_pin16, n74244_1_pin18,
       n74244_2_pin1, n74244_3_pin11, n74244_7_pin3, n74244_7_pin5, n74244_7_pin7, n74244_7_pin9,
       n74244_7_pin12, n74244_7_pin14, n74244_7_pin16, n74244_7_pin18, nand_1_out, nand_2_out, nand_3_out,
       nand_4_out, nand_5_out, nand_6_out, nand_7_out, nand_8_out, nand_9_out, nor_1_out, nor_2_out,
       nor_3_out, nor_4_out, nor_5_out, nor_6_out, nor_7_out, nor_8_out, not_1_out, not_2_out, not_3_out,
       not_4_out, not_8_out, not_9_out, not_10_out, or_1_out, pull_resistor_1_node, pull_resistor_20_node,
       pull_resistor_21_node;
  wire [7:0] adder_1_out, n74240_4_pin9;

  // Probe on result
  // Probe on {status[3:1], result[7]}
  Pull_Resistor pull_resistor_1 (.node(pull_resistor_1_node));
  _74240 u_74240_1 (
    .pin1(pull_resistor_1_node), .pin2(s[0]), .pin4(s[1]), .pin6(s[2]), .pin8(s[3]),
    .pin19(pull_resistor_1_node), .pin18(n74240_1_pin18), .pin16(n74240_1_pin16), .pin14(n74240_1_pin14),
    .pin12(n74240_1_pin12));  // open: pin3, pin5, pin7, pin9, pin17, pin15, pin13, pin11
  nor nor_1 (nor_1_out, x[0], y[0]);
  nor nor_2 (nor_2_out, x[1], y[1]);
  nor nor_3 (nor_3_out, x[2], y[2]);
  nor nor_4 (nor_4_out, x[3], y[3]);
  nor nor_5 (nor_5_out, x[4], y[4]);
  nor nor_6 (nor_6_out, x[5], y[5]);
  nor nor_7 (nor_7_out, x[6], y[6]);
  nor nor_8 (nor_8_out, x[7], y[7]);
  _74240 u_74240_2 (
    .pin1(n74240_2_pin1), .pin2(nor_5_out), .pin3(result[3]), .pin4(nor_6_out), .pin5(result[2]),
    .pin6(nor_7_out), .pin7(result[1]), .pin8(nor_8_out), .pin9(result[0]), .pin19(n74240_2_pin1),
    .pin18(result[4]), .pin17(nor_4_out), .pin16(result[5]), .pin15(nor_3_out), .pin14(result[6]),
    .pin13(nor_2_out), .pin12(result[7]), .pin11(nor_1_out));
  _7420 u_7420_1 (
    .pin1(s[0]), .pin2(n74240_1_pin16), .pin4(s[2]), .pin5(s[3]), .pin6(n74240_2_pin1),
    .pin13(n74240_1_pin16), .pin12(n74240_1_pin18), .pin10(s[3]), .pin9(s[2]), .pin8(n7420_1_pin8));  // open: pin3, pin11
  nand nand_1 (nand_1_out, x[0], y[0]);
  nand nand_2 (nand_2_out, x[1], y[1]);
  nand nand_3 (nand_3_out, x[2], y[2]);
  nand nand_4 (nand_4_out, x[3], y[3]);
  nand nand_5 (nand_5_out, x[4], y[4]);
  nand nand_6 (nand_6_out, x[5], y[5]);
  nand nand_7 (nand_7_out, x[6], y[6]);
  nand nand_8 (nand_8_out, x[7], y[7]);
  _74240 u_74240_3 (
    .pin1(n7420_1_pin8), .pin2(nand_5_out), .pin3(result[3]), .pin4(nand_6_out), .pin5(result[2]),
    .pin6(nand_7_out), .pin7(result[1]), .pin8(nand_8_out), .pin9(result[0]), .pin19(n7420_1_pin8),
    .pin18(result[4]), .pin17(nand_4_out), .pin16(result[5]), .pin15(nand_3_out), .pin14(result[6]),
    .pin13(nand_2_out), .pin12(result[7]), .pin11(nand_1_out));
  Pull_Resistor #(.pull(1)) pull_resistor_2 (.node(result[7]));
  Pull_Resistor #(.pull(1)) pull_resistor_3 (.node(result[6]));
  Pull_Resistor #(.pull(1)) pull_resistor_4 (.node(result[5]));
  _74244 u_74244_1 (
    .pin1(s[0]), .pin2(y[7]), .pin3(n74244_1_pin3), .pin4(y[6]), .pin5(n74244_1_pin5), .pin6(y[1]),
    .pin7(n74244_1_pin7), .pin8(y[0]), .pin9(n74244_1_pin9), .pin19(s[0]), .pin18(n74244_1_pin18),
    .pin17(y[2]), .pin16(n74244_1_pin16), .pin15(y[3]), .pin14(n74244_1_pin14), .pin13(y[4]),
    .pin12(n74244_1_pin12), .pin11(y[5]));
  Pull_Resistor #(.pull(1)) pull_resistor_5 (.node(result[4]));
  Pull_Resistor #(.pull(1)) pull_resistor_6 (.node(result[3]));
  Pull_Resistor #(.pull(1)) pull_resistor_7 (.node(result[2]));
  Pull_Resistor #(.pull(1)) pull_resistor_8 (.node(result[1]));
  Pull_Resistor #(.pull(1)) pull_resistor_9 (.node(n74244_1_pin18));
  Pull_Resistor #(.pull(1)) pull_resistor_10 (.node(n74244_1_pin16));
  Pull_Resistor #(.pull(1)) pull_resistor_11 (.node(n74244_1_pin14));
  Pull_Resistor #(.pull(1)) pull_resistor_12 (.node(n74244_1_pin12));
  Pull_Resistor #(.pull(1)) pull_resistor_13 (.node(n74244_1_pin9));
  Pull_Resistor #(.pull(1)) pull_resistor_14 (.node(n74244_1_pin7));
  Pull_Resistor #(.pull(1)) pull_resistor_15 (.node(n74244_1_pin5));
  Pull_Resistor #(.pull(1)) pull_resistor_16 (.node(n74244_1_pin3));
  Pull_Resistor #(.pull(1)) pull_resistor_17 (.node(result[0]));
  _7486 u_7486_1 (
    .pin1(x[7]), .pin2(n74244_1_pin18), .pin3(n7486_1_pin3), .pin4(n74244_1_pin16), .pin5(x[6]),
    .pin6(n7486_1_pin6), .pin13(x[0]), .pin12(n74244_1_pin12), .pin11(n7486_1_pin11), .pin10(n74244_1_pin14),
    .pin9(x[1]), .pin8(n7486_1_pin8));
  _7486 u_7486_2 (
    .pin1(x[5]), .pin2(n74244_1_pin9), .pin3(n7486_2_pin3), .pin4(n74244_1_pin7), .pin5(x[4]),
    .pin6(n7486_2_pin6), .pin13(x[2]), .pin12(n74244_1_pin3), .pin11(n7486_2_pin11), .pin10(n74244_1_pin5),
    .pin9(x[3]), .pin8(n7486_2_pin8));
  _74244 u_74244_2 (
    .pin1(n74244_2_pin1), .pin2(n7486_2_pin6), .pin3(result[3]), .pin4(n7486_2_pin3), .pin5(result[2]),
    .pin6(n7486_1_pin6), .pin7(result[1]), .pin8(n7486_1_pin3), .pin9(result[0]), .pin19(n74244_2_pin1),
    .pin18(result[4]), .pin17(n7486_2_pin8), .pin16(result[5]), .pin15(n7486_2_pin11), .pin14(result[6]),
    .pin13(n7486_1_pin8), .pin12(result[7]), .pin11(n7486_1_pin11));
  _7420 u_7420_2 (
    .pin1(s[1]), .pin2(s[2]), .pin4(n7420_2_pin4), .pin5(s[3]), .pin6(n74244_2_pin1), .pin13(n74240_1_pin18),
    .pin12(n74240_1_pin16), .pin10(s[3]), .pin9(n74240_1_pin14), .pin8(n7420_2_pin8));  // open: pin3, pin11
  Pull_Resistor #(.pull(1)) pull_resistor_18 (.node(n7420_2_pin4));
  _74244 u_74244_3 (
    .pin1(n7420_2_pin8), .pin2(x[3]), .pin3(result[3]), .pin4(x[4]), .pin5(result[2]), .pin6(x[5]),
    .pin7(result[1]), .pin8(x[6]), .pin9(result[0]), .pin19(n7420_2_pin8), .pin18(result[4]), .pin17(x[2]),
    .pin16(result[5]), .pin15(x[1]), .pin14(result[6]), .pin13(x[0]), .pin12(result[7]),
    .pin11(n74244_3_pin11));
  not not_1 (not_1_out, n7420_2_pin8);
  nand nand_9 (nand_9_out, not_1_out, x[7]);
  Pull_Resistor pull_resistor_19 (.node(n74244_3_pin11));
  not not_2 (not_2_out, n7410_1_pin8);
  nand nand_10 (nand_9_out, x[0], not_3_out);
  Pull_Resistor #(.pull(1)) pull_resistor_20 (.node(pull_resistor_20_node));
  _7410 u_7410_1 (
    .pin1(s[3]), .pin2(s[0]), .pin3(n74240_1_pin12), .pin4(s[2]), .pin5(pull_resistor_20_node),
    .pin6(n7410_1_pin6), .pin13(n74240_1_pin14), .pin12(n7410_1_pin12), .pin11(x[7]),
    .pin10(pull_resistor_20_node), .pin9(n74240_1_pin16), .pin8(n7410_1_pin8));
  not not_3 (not_3_out, n7410_1_pin12);
  _74244 u_74244_4 (
    .pin1(n7410_1_pin12), .pin2(x[5]), .pin3(result[3]), .pin4(x[6]), .pin5(result[2]), .pin6(x[7]),
    .pin7(result[1]), .pin8(not_2_out), .pin9(result[0]), .pin19(n7410_1_pin12), .pin18(result[4]),
    .pin17(x[4]), .pin16(result[5]), .pin15(x[3]), .pin14(result[6]), .pin13(x[2]), .pin12(result[7]),
    .pin11(x[1]));
  not not_4 (not_4_out, n7402_1_pin3);
  _7402 u_7402_1 (
    .pin1(n7402_1_pin1), .pin2(n7402_1_pin2), .pin3(n7402_1_pin3), .pin4(n7402_1_pin4), .pin5(n7402_1_pin5),
    .pin6(n7402_1_pin6), .pin13(n7402_1_pin2), .pin12(n7402_1_pin12), .pin11(n7402_1_pin11),
    .pin10(n7402_1_pin10), .pin9(n7402_1_pin11), .pin8(n7402_1_pin8));
  not not_5 (n7402_1_pin6, x[7]);
  _74244 u_74244_5 (
    .pin1(n7402_1_pin1), .pin2(x[4]), .pin3(result[3]), .pin4(x[5]), .pin5(result[2]), .pin6(x[6]),
    .pin7(result[1]), .pin8(n7402_1_pin4), .pin9(result[0]), .pin19(n7402_1_pin1), .pin18(result[4]),
    .pin17(x[3]), .pin16(result[5]), .pin15(x[2]), .pin14(result[6]), .pin13(x[1]), .pin12(result[7]),
    .pin11(x[0]));
  Pull_Resistor pull_resistor_21 (.node(pull_resistor_21_node));
  _7427 u_7427_1 (
    .pin1(n74240_1_pin18), .pin2(pull_resistor_21_node), .pin3(s[2]), .pin4(n74240_1_pin16), .pin5(s[0]),
    .pin6(n7427_1_pin6), .pin13(not_4_out), .pin12(n7402_1_pin5), .pin11(s[3]), .pin10(s[2]), .pin9(s[1]),
    .pin8(n7402_1_pin3));
  not not_6 (n7402_1_pin11, n7427_1_pin6);
  _7486 u_7486_3 (
    .pin13(s[1]), .pin12(x[7]), .pin11(n7486_3_pin11), .pin10(n74240_1_pin12), .pin9(adder_1_out[7]),
    .pin8(n7402_1_pin12));  // open: pin1, pin2, pin3, pin4, pin5, pin6
  not not_7 (n7402_1_pin8, n7402_1_pin12);
  not not_8 (not_8_out, n7402_1_pin10);
  _74244 u_74244_6 (
    .pin1(not_8_out), .pin2(y[4]), .pin3(result[3]), .pin4(y[5]), .pin5(result[2]), .pin6(y[6]),
    .pin7(result[1]), .pin8(y[7]), .pin9(result[0]), .pin19(not_8_out), .pin18(result[4]), .pin17(y[3]),
    .pin16(result[5]), .pin15(y[2]), .pin14(result[6]), .pin13(y[1]), .pin12(result[7]), .pin11(y[0]));
  _74244 u_74244_7 (
    .pin1(s[0]), .pin2(y[0]), .pin3(n74244_7_pin3), .pin4(y[1]), .pin5(n74244_7_pin5), .pin6(y[2]),
    .pin7(n74244_7_pin7), .pin8(y[3]), .pin9(n74244_7_pin9), .pin19(s[0]), .pin18(n74244_7_pin18),
    .pin17(y[7]), .pin16(n74244_7_pin16), .pin15(y[6]), .pin14(n74244_7_pin14), .pin13(y[5]),
    .pin12(n74244_7_pin12), .pin11(y[4]));
  _74240 u_74240_4 (
    .pin1(n74240_4_pin1), .pin2(n74244_7_pin9), .pin3(n74240_4_pin9[3]), .pin4(n74244_7_pin7),
    .pin5(n74240_4_pin9[2]), .pin6(n74244_7_pin5), .pin7(n74240_4_pin9[1]), .pin8(n74244_7_pin3),
    .pin9(n74240_4_pin9[0]), .pin19(n74240_4_pin1), .pin18(n74240_4_pin9[4]), .pin17(n74244_7_pin12),
    .pin16(n74240_4_pin9[5]), .pin15(n74244_7_pin14), .pin14(n74240_4_pin9[6]), .pin13(n74244_7_pin16),
    .pin12(n74240_4_pin9[7]), .pin11(n74244_7_pin18));
  nor nor_9 (n74240_4_pin1, s[1], n7427_1_pin6);
  Pull_Resistor #(.pull(1)) pull_resistor_22 (.node(n74244_7_pin18));
  Pull_Resistor pull_resistor_23 (.node(n74244_7_pin16));
  Pull_Resistor pull_resistor_24 (.node(n74244_7_pin14));
  Pull_Resistor pull_resistor_25 (.node(n74244_7_pin12));
  not not_9 (not_9_out, n74240_4_pin1);
  _74244 u_74244_8 (
    .pin1(not_9_out), .pin2(n74244_7_pin9), .pin3(n74240_4_pin9[3]), .pin4(n74244_7_pin7),
    .pin5(n74240_4_pin9[2]), .pin6(n74244_7_pin5), .pin7(n74240_4_pin9[1]), .pin8(n74244_7_pin3),
    .pin9(n74240_4_pin9[0]), .pin19(not_9_out), .pin18(n74240_4_pin9[4]), .pin17(n74244_7_pin12),
    .pin16(n74240_4_pin9[5]), .pin15(n74244_7_pin14), .pin14(n74240_4_pin9[6]), .pin13(n74244_7_pin16),
    .pin12(n74240_4_pin9[7]), .pin11(n74244_7_pin18));
  not not_10 (not_10_out, adder_1_out[7]);
  or or_1 (or_1_out, y[7], not_10_out, n7486_3_pin11);
  Pull_Resistor pull_resistor_26 (.node(n74244_7_pin9));
  Pull_Resistor pull_resistor_27 (.node(n74244_7_pin7));
  Pull_Resistor pull_resistor_28 (.node(n74244_7_pin5));
  Pull_Resistor pull_resistor_29 (.node(n74244_7_pin3));
  _7410 u_7410_2 (
    .pin1(not_10_out), .pin2(y[7]), .pin3(n7410_2_pin3), .pin4(or_1_out), .pin5(n7410_2_pin5),
    .pin6(n7410_2_pin6), .pin13(n7486_3_pin11), .pin12(n7410_2_pin3), .pin11(n7410_2_pin11),
    .pin10(n7410_2_pin10), .pin9(n7410_2_pin6), .pin8(n7410_2_pin8));
  Pull_Resistor #(.pull(1)) pull_resistor_30 (.node(n7410_2_pin5));
  Adder adder_1 (.a(x), .b(n74240_4_pin9), .out(adder_1_out), .cin(not_9_out), .cout(n7410_2_pin10));
  not not_11 (n7410_2_pin11, n7410_1_pin6);
  assign nand_9_out = n7410_2_pin11 ? ~n7410_2_pin10 : 1'bz;  // Controlled_Inverter controlled_inverter_1
  Pull_Resistor #(.pull(1)) pull_resistor_31 (.node(nand_9_out));
  not not_12 (status[2], nand_9_out);
  not not_13 (status[3], n7410_2_pin8);
  _74244 u_74244_9 (
    .pin1(n7410_1_pin6), .pin2(adder_1_out[4]), .pin3(result[3]), .pin4(adder_1_out[5]), .pin5(result[2]),
    .pin6(adder_1_out[6]), .pin7(result[1]), .pin8(adder_1_out[7]), .pin9(result[0]), .pin19(n7410_1_pin6),
    .pin18(result[4]), .pin17(adder_1_out[3]), .pin16(result[5]), .pin15(adder_1_out[2]), .pin14(result[6]),
    .pin13(adder_1_out[1]), .pin12(result[7]), .pin11(adder_1_out[0]));
  nor nor_10 (status[1], result[0], result[1], result[2], result[3], result[4], result[5], result[6], result[7]);

  assign status[0] = result[7];

  // Notes on the sheet:
  //   OR
  //   AND
  //   XOR / INV
  //   7
  //   6
  //   1
  //   0
  //   2
  //   3
  //   4
  //   5
  //   nand_9 drives only 0 and floats otherwise
  //   shl
  //   nand_10 drives only 0 and floats otherwise
  //   shr
  //   take x
  //   take y
  //   0
  //   1
  //   2
  //   3
  //   4
  //   5
  //   6
  //   7
  //   N negative
  //   Z zero
  //   C carry out
  //   V overflow
endmodule

module overflow (
  input  sub,
  input  x,
  input  y,
  input  r
);

  wire nand_1_out, not_1_out, or_1_out, xor_1_out;

  xor xor_1 (xor_1_out, sub, x);
  not not_1 (not_1_out, r);
  or or_1 (or_1_out, xor_1_out, y, not_1_out);
  nand nand_1 (nand_1_out, y, xor_1_out, not_1_out);
  // NAND_Gate nand_2 has open pins: in0=or_1_out, in1=nand_1_out, out=open
endmodule

module DecoderUnit (
  input  [15:0] opcode,
  output [3:0] sel,
  output [3:0] alu,
  output [7:0] data,
  output [3:0] con,
  output [2:0] adr,
  output mode
);


  assign adr = opcode[14:12];
  assign alu = opcode[7:4];
  assign con = opcode[11:8];
  assign data = opcode[7:0];
  assign mode = opcode[15];
  assign sel = opcode[3:0];
endmodule

module RegisterSelectUnit (
  input  [3:0] s,
  input  [7:0] A,
  input  [7:0] HI,
  input  [7:0] LO,
  input  [7:0] P,
  input  [7:0] D,
  input  [7:0] RAM,
  input  [7:0] SP,
  output [7:0] x,
  output [7:0] y
);

  wire nand_1_out, nand_2_out, nand_3_out, nand_4_out, nand_5_out, nand_6_out, nand_7_out, not_1_out,
       not_2_out, not_3_out, not_4_out, not_5_out, not_6_out, not_7_out, not_8_out, not_9_out, not_10_out,
       not_11_out, undriven, xor_1_out;
  wire [7:0] controlled_buffer_1_out, controlled_buffer_3_out;

  not not_1 (not_1_out, s[2]);
  not not_2 (not_2_out, s[1]);
  not not_3 (not_3_out, s[0]);
  nand nand_1 (nand_1_out, s[1], s[2]);
  nand nand_2 (nand_2_out, s[0], not_2_out, s[2]);
  nand nand_3 (nand_3_out, not_3_out, not_2_out, s[2]);
  nand nand_4 (nand_4_out, s[0], s[1], not_1_out);
  nand nand_5 (nand_5_out, not_3_out, not_2_out, not_1_out);
  nand nand_6 (nand_6_out, not_3_out, s[1]);
  xor xor_1 (xor_1_out, s[1], s[2]);
  not not_4 (not_4_out, nand_2_out);
  not not_5 (not_5_out, nand_3_out);
  not not_6 (not_6_out, nand_4_out);
  not not_7 (not_7_out, nand_5_out);
  not not_8 (not_8_out, nand_6_out);
  not not_9 (not_9_out, xor_1_out);
  not not_10 (not_10_out, nand_1_out);
  assign controlled_buffer_1_out = nand_1_out ? A : 8'bz;  // Controlled_Buffer controlled_buffer_1
  assign controlled_buffer_1_out = not_10_out ? D : 8'bz;  // Controlled_Buffer controlled_buffer_2
  assign controlled_buffer_3_out = not_4_out ? HI : 8'bz;  // Controlled_Buffer controlled_buffer_3
  assign controlled_buffer_3_out = not_5_out ? LO : 8'bz;  // Controlled_Buffer controlled_buffer_4
  assign controlled_buffer_3_out = not_6_out ? P : 8'bz;  // Controlled_Buffer controlled_buffer_5
  assign controlled_buffer_3_out = not_7_out ? D : 8'bz;  // Controlled_Buffer controlled_buffer_6
  assign controlled_buffer_3_out = not_8_out ? RAM : 8'bz;  // Controlled_Buffer controlled_buffer_7
  assign controlled_buffer_3_out = not_11_out ? SP : 8'bz;  // Controlled_Buffer controlled_buffer_8
  nand nand_7 (nand_7_out, s[0], not_9_out);
  not not_11 (not_11_out, nand_7_out);
  Controlled_Buffer #(.width(8)) controlled_buffer_9 (.in(controlled_buffer_3_out), .out(x));  // open: en
  assign x = undriven ? controlled_buffer_1_out : 8'bz;  // Controlled_Buffer controlled_buffer_10
  assign y = undriven ? controlled_buffer_1_out : 8'bz;  // Controlled_Buffer controlled_buffer_11
  Controlled_Buffer #(.width(8)) controlled_buffer_12 (.in(controlled_buffer_3_out), .out(y));  // open: en
endmodule

module ConditionUnit (
  input  [3:0] s,
  input  [3:0] status,
  output r
);

  wire and_1_out, and_2_out, nor_1_out, not_1_out, not_2_out, pull_resistor_1_node, select_1_of_8_1_out_4,
       select_1_of_8_1_out_5, select_1_of_8_1_out_6, select_1_of_8_1_out_7, select_1_of_8_1_out_8,
       select_1_of_8_1_out_9, select_1_of_8_1_out_10, select_1_of_8_1_out_11;

  nor nor_1 (nor_1_out, status[1], status[0]);
  not not_1 (not_1_out, status[0]);
  and and_1 (and_1_out, not_1_out, status[3]);
  and and_2 (and_2_out, status[0], status[3]);
  // NoConnect on select_1_of_8_1_out_4
  select_1_of_8 select_1_of_8_1 (
    .s2(s[2]), .s1(s[1]), .s0(s[0]), .out_4(select_1_of_8_1_out_4), .out_5(select_1_of_8_1_out_5),
    .out_6(select_1_of_8_1_out_6), .out_7(select_1_of_8_1_out_7), .out_8(select_1_of_8_1_out_8),
    .out_9(select_1_of_8_1_out_9), .out_10(select_1_of_8_1_out_10), .out_11(select_1_of_8_1_out_11));
  Pull_Resistor #(.pull(1)) pull_resistor_1 (.node(pull_resistor_1_node));
  nand nand_1 (pull_resistor_1_node, select_1_of_8_1_out_5, status[0]);
  nand nand_2 (pull_resistor_1_node, select_1_of_8_1_out_6, status[1]);
  nand nand_3 (pull_resistor_1_node, select_1_of_8_1_out_7, nor_1_out);
  nand nand_4 (pull_resistor_1_node, select_1_of_8_1_out_8, status[2]);
  nand nand_5 (pull_resistor_1_node, select_1_of_8_1_out_9, and_1_out);
  nand nand_6 (pull_resistor_1_node, select_1_of_8_1_out_10, and_2_out);
  nand nand_7 (pull_resistor_1_node, select_1_of_8_1_out_11, status[3]);
  not not_2 (not_2_out, s[3]);
  xor xor_1 (r, not_2_out, pull_resistor_1_node);

  // Notes on the sheet:
  //   N negative
  //   Z zero
  //   C carry out
  //   V overflow
  //   nand_1 drives only 0 and floats otherwise
  //   nand_2 drives only 0 and floats otherwise
  //   nand_3 drives only 0 and floats otherwise
  //   nand_4 drives only 0 and floats otherwise
  //   nand_5 drives only 0 and floats otherwise
  //   nand_6 drives only 0 and floats otherwise
  //   nand_7 drives only 0 and floats otherwise
endmodule

module RegisterBank (
  input  [7:0] data,
  input  [2:0] adr,
  input  clock,
  input  reset,
  input  sINdata,
  input  sINclock,
  input  sync,
  output [7:0] LOout,
  output [7:0] RAMout,
  output [7:0] HIout,
  output [7:0] SPout,
  output [7:0] Pout,
  output [7:0] Aout,
  output [7:0] Dout,
  output DISout,
  output DIStick
);

  wire nor_1_out, select_1_of_8_1_out_4, select_1_of_8_1_out_5, select_1_of_8_1_out_6, select_1_of_8_1_out_7,
       select_1_of_8_1_out_8, select_1_of_8_1_out_9, select_1_of_8_1_out_10, select_1_of_8_1_out_11;
  wire [7:0] deserialise_8_1_data;

  // NoConnect on select_1_of_8_1_out_4
  select_1_of_8 select_1_of_8_1 (
    .s2(adr[2]), .s1(adr[1]), .s0(adr[0]), .out_4(select_1_of_8_1_out_4), .out_5(select_1_of_8_1_out_5),
    .out_6(select_1_of_8_1_out_6), .out_7(select_1_of_8_1_out_7), .out_8(select_1_of_8_1_out_8),
    .out_9(select_1_of_8_1_out_9), .out_10(select_1_of_8_1_out_10), .out_11(select_1_of_8_1_out_11));
  Register LO (.D(data), .en(select_1_of_8_1_out_5), .clk(clock), .Q(LOout), .clr(reset));
  Register HI (.D(data), .en(select_1_of_8_1_out_6), .clk(clock), .Q(HIout), .clr(reset));
  Register SP (.D(data), .en(select_1_of_8_1_out_8), .clk(clock), .Q(SPout), .clr(reset));
  Register A (.D(data), .en(select_1_of_8_1_out_9), .clk(clock), .Q(Aout), .clr(reset));
  Register D (.D(data), .en(select_1_of_8_1_out_10), .clk(clock), .Q(Dout), .clr(reset));
  serialise_8 serialise_8_1 (
    .start(select_1_of_8_1_out_11), .clock(clock), .data(data), .tick(DIStick), .serial(DISout));
  RAM #(.addrWidth(13)) ram_1 (
    .addr({HIout[4:0], LOout}), .we(select_1_of_8_1_out_7), .oe(1'b1), .clk(clock), .din(data), .dout(RAMout));
  deserialise_8 deserialise_8_1 (.serial(sINdata), .clock(sINclock), .data(deserialise_8_1_data));  // open: reset
  nor nor_1 (nor_1_out, HIout[5], HIout[6]);
  hw_timer hw_timer_1 (.reset(reset), .tick(sync), .active(HIout[6]), .switch(HIout[5]), .timestamp(Pout));
  Pull_Resistor pull_resistor_1 (.node(Pout));
  assign Pout = nor_1_out ? deserialise_8_1_data : 8'bz;  // Controlled_Buffer controlled_buffer_1
endmodule

module ProgramCounter (
  input  [15:0] override,
  input  reset,
  input  clock,
  input  jmp,
  output [15:0] adr
);

  wire n74161_1_pin7, n74161_1_pin15, n74161_2_pin7, n74161_2_pin15, n74161_3_pin7, n74161_3_pin15,
       n74161_4_pin7, n74161_4_pin15, nand_1_out, nand_2_out, nand_3_out, not_1_out, not_2_out, not_3_out,
       or_1_out, or_2_out, or_3_out;

  not not_1 (not_1_out, jmp);
  not not_2 (not_2_out, reset);
  not not_3 (not_3_out, clock);
  _74161 u_74161_1 (
    .pin1(not_2_out), .pin2(not_3_out), .pin3(override[0]), .pin4(override[1]), .pin5(override[2]),
    .pin6(override[3]), .pin7(n74161_1_pin7), .pin15(n74161_1_pin15), .pin14(adr[0]), .pin13(adr[1]),
    .pin12(adr[2]), .pin11(adr[3]), .pin10(n74161_1_pin7), .pin9(not_1_out));
  or or_1 (or_1_out, jmp, n74161_1_pin15);
  nand nand_1 (nand_1_out, or_1_out, clock);
  _74161 u_74161_2 (
    .pin1(not_2_out), .pin2(nand_1_out), .pin3(override[4]), .pin4(override[5]), .pin5(override[6]),
    .pin6(override[7]), .pin7(n74161_2_pin7), .pin15(n74161_2_pin15), .pin14(adr[4]), .pin13(adr[5]),
    .pin12(adr[6]), .pin11(adr[7]), .pin10(n74161_2_pin7), .pin9(not_1_out));
  or or_2 (or_2_out, jmp, n74161_2_pin15);
  nand nand_2 (nand_2_out, or_2_out, clock);
  _74161 u_74161_3 (
    .pin1(not_2_out), .pin2(nand_2_out), .pin3(override[8]), .pin4(override[9]), .pin5(override[10]),
    .pin6(override[11]), .pin7(n74161_3_pin7), .pin15(n74161_3_pin15), .pin14(adr[8]), .pin13(adr[9]),
    .pin12(adr[10]), .pin11(adr[11]), .pin10(n74161_3_pin7), .pin9(not_1_out));
  or or_3 (or_3_out, jmp, n74161_3_pin15);
  nand nand_3 (nand_3_out, or_3_out, clock);
  _74161 u_74161_4 (
    .pin1(not_2_out), .pin2(nand_3_out), .pin3(override[12]), .pin4(override[13]), .pin5(override[14]),
    .pin6(override[15]), .pin7(n74161_4_pin7), .pin15(n74161_4_pin15), .pin14(adr[12]), .pin13(adr[13]),
    .pin12(adr[14]), .pin11(adr[15]), .pin10(n74161_4_pin7), .pin9(not_1_out));
  // NoConnect on n74161_4_pin15
  // also tied to VCC on the sheet: {n74161_1_pin7, n74161_2_pin7, n74161_3_pin7, n74161_4_pin7}

  // Notes on the sheet:
  //   override: initial=0x2a
endmodule

module KeyboardBuffer (
  input  [7:0] a,
  input  reset,
  output [7:0] q
);

  D_Flip_Flop d_ff_1 (.Q(q[0]), .preset(a[0]), .reset(reset));  // open: D, clk, Qn
  D_Flip_Flop d_ff_2 (.Q(q[1]), .preset(a[1]), .reset(reset));  // open: D, clk, Qn
  D_Flip_Flop d_ff_3 (.Q(q[2]), .preset(a[2]), .reset(reset));  // open: D, clk, Qn
  D_Flip_Flop d_ff_4 (.Q(q[3]), .preset(a[3]), .reset(reset));  // open: D, clk, Qn
  D_Flip_Flop d_ff_5 (.Q(q[4]), .preset(a[4]), .reset(reset));  // open: D, clk, Qn
  D_Flip_Flop d_ff_6 (.Q(q[5]), .preset(a[5]), .reset(reset));  // open: D, clk, Qn
  D_Flip_Flop d_ff_7 (.Q(q[6]), .preset(a[6]), .reset(reset));  // open: D, clk, Qn
  D_Flip_Flop d_ff_8 (.Q(q[7]), .preset(a[7]), .reset(reset));  // open: D, clk, Qn
endmodule

module MatrixController_16p (
  input  serial,
  input  clock,
  output [15:0] anode,
  output [15:0] kathode,
  output ll
);

  wire deserialise_16_1_lb, n74161_1_pin1, n74161_1_pin2, n74161_1_pin3, n74161_1_pin7, n74161_1_pin11,
       n74161_1_pin12, n74161_1_pin13, n74161_1_pin14, n74161_1_pin15;

  deserialise_16 deserialise_16_1 (
    .serial(serial), .clock(clock), .lb(deserialise_16_1_lb), .data(anode));  // open: reset
  _74161 u_74161_1 (
    .pin1(n74161_1_pin1), .pin2(n74161_1_pin2), .pin3(n74161_1_pin3), .pin4(n74161_1_pin3),
    .pin5(n74161_1_pin3), .pin6(n74161_1_pin3), .pin7(n74161_1_pin7), .pin15(n74161_1_pin15),
    .pin14(n74161_1_pin14), .pin13(n74161_1_pin13), .pin12(n74161_1_pin12), .pin11(n74161_1_pin11),
    .pin10(n74161_1_pin7), .pin9(n74161_1_pin7));
  Pull_Resistor #(.pull(1)) pull_resistor_1 (.node(n74161_1_pin1));
  not not_1 (n74161_1_pin2, deserialise_16_1_lb);
  Pull_Resistor pull_resistor_2 (.node(n74161_1_pin3));
  Pull_Resistor #(.pull(1)) pull_resistor_3 (.node(n74161_1_pin7));
  // NoConnect on n74161_1_pin15
  and and_1 (ll, n74161_1_pin11, n74161_1_pin12, n74161_1_pin13, n74161_1_pin14);
  select_1_of_16 select_1_of_16_1 (
    .s3(n74161_1_pin11), .s2(n74161_1_pin12), .s1(n74161_1_pin13), .s0(n74161_1_pin14), .out_5(kathode[0]),
    .out_6(kathode[1]), .out_7(kathode[2]), .out_8(kathode[3]), .out_9(kathode[4]), .out_10(kathode[5]),
    .out_11(kathode[6]), .out_12(kathode[7]), .out_13(kathode[8]), .out_14(kathode[9]), .out_15(kathode[10]),
    .out_16(kathode[11]), .out_17(kathode[12]), .out_18(kathode[13]), .out_19(kathode[14]),
    .out_20(kathode[15]));
endmodule

module serialise_8 (
  input  start,
  input  [7:0] data,
  input  clock,
  output tick,
  output serial
);

  wire n74161_1_pin3, n74161_1_pin7, n74161_1_pin11, n74161_1_pin12, n74161_1_pin13, n74161_1_pin14,
       n74161_1_pin15, n74165_1_pin7, n74165_1_pin10, n74165_1_pin15, nor_1_out, not_1_out, not_2_out;

  not not_1 (not_1_out, start);
  not not_2 (not_2_out, clock);
  _74165 u_74165_1 (
    .pin1(not_1_out), .pin2(clock), .pin3(data[4]), .pin4(data[5]), .pin5(data[6]), .pin6(data[7]),
    .pin7(n74165_1_pin7), .pin15(n74165_1_pin15), .pin14(data[3]), .pin13(data[2]), .pin12(data[1]),
    .pin11(data[0]), .pin10(n74165_1_pin10), .pin9(serial));
  // NoConnect on n74165_1_pin7
  nor nor_1 (nor_1_out, not_2_out, n74165_1_pin15);
  nor nor_2 (tick, n74165_1_pin15, nor_1_out);
  _74161 u_74161_1 (
    .pin1(not_1_out), .pin2(nor_1_out), .pin3(n74161_1_pin3), .pin4(n74161_1_pin3), .pin5(n74161_1_pin3),
    .pin6(n74161_1_pin3), .pin7(n74161_1_pin7), .pin15(n74161_1_pin15), .pin14(n74161_1_pin14),
    .pin13(n74161_1_pin13), .pin12(n74161_1_pin12), .pin11(n74161_1_pin11), .pin10(n74161_1_pin7),
    .pin9(n74161_1_pin7));
  // NoConnect on n74161_1_pin15
  // NoConnect on n74161_1_pin11
  and and_1 (n74165_1_pin15, n74161_1_pin12, n74161_1_pin13, n74161_1_pin14);
  // also tied to GND on the sheet: {n74165_1_pin10, n74161_1_pin3}
  // also tied to VCC on the sheet: n74161_1_pin7
endmodule

module deserialise_8 (
  input  serial,
  input  clock,
  input  reset,
  output [7:0] data
);

  wire n74161_1_pin11, n74161_1_pin12, n74161_1_pin13, n74161_1_pin14, n74161_1_pin15, n74164_1_pin3,
       n74164_1_pin4, n74164_1_pin5, n74164_1_pin6, n74164_1_pin10, n74164_1_pin11, n74164_1_pin12,
       n74164_1_pin13, n74377_1_pin1, nor_1_out, nor_2_out, not_1_out, not_2_out, not_3_out,
       pull_resistor_1_node, pull_resistor_2_node, pull_resistor_3_node;

  not not_1 (not_1_out, n74161_1_pin11);
  Pull_Resistor #(.pull(1)) pull_resistor_1 (.node(pull_resistor_1_node));
  nor nor_1 (nor_1_out, reset, nor_2_out);
  nor nor_2 (nor_2_out, clock, not_1_out);
  Pull_Resistor pull_resistor_2 (.node(pull_resistor_2_node));
  Pull_Resistor #(.pull(1)) pull_resistor_3 (.node(pull_resistor_3_node));
  _74164 u_74164_1 (
    .pin1(pull_resistor_1_node), .pin2(serial), .pin3(n74164_1_pin3), .pin4(n74164_1_pin4),
    .pin5(n74164_1_pin5), .pin6(n74164_1_pin6), .pin13(n74164_1_pin13), .pin12(n74164_1_pin12),
    .pin11(n74164_1_pin11), .pin10(n74164_1_pin10), .pin9(pull_resistor_1_node), .pin8(clock));
  not not_2 (not_2_out, clock);
  _74161 u_74161_1 (
    .pin1(nor_1_out), .pin2(not_2_out), .pin3(pull_resistor_2_node), .pin4(pull_resistor_2_node),
    .pin5(pull_resistor_2_node), .pin6(pull_resistor_2_node), .pin7(pull_resistor_3_node),
    .pin15(n74161_1_pin15), .pin14(n74161_1_pin14), .pin13(n74161_1_pin13), .pin12(n74161_1_pin12),
    .pin11(n74161_1_pin11), .pin10(pull_resistor_3_node), .pin9(pull_resistor_3_node));
  // NoConnect on n74161_1_pin15
  // NoConnect on n74161_1_pin14
  // NoConnect on n74161_1_pin13
  // NoConnect on n74161_1_pin12
  not not_3 (not_3_out, n74161_1_pin11);
  _74377 u_74377_1 (
    .pin1(n74377_1_pin1), .pin2(data[0]), .pin3(n74164_1_pin13), .pin4(n74164_1_pin12), .pin5(data[1]),
    .pin6(data[2]), .pin7(n74164_1_pin11), .pin8(n74164_1_pin10), .pin9(data[3]), .pin19(data[4]),
    .pin18(n74164_1_pin3), .pin17(n74164_1_pin4), .pin16(data[5]), .pin15(data[6]), .pin14(n74164_1_pin5),
    .pin13(n74164_1_pin6), .pin12(data[7]), .pin11(not_3_out));
  Pull_Resistor pull_resistor_4 (.node(n74377_1_pin1));
endmodule

module deserialise_16 (
  input  serial,
  input  clock,
  input  reset,
  output [15:0] data,
  output lb
);

  wire n74161_1_pin1, n74161_1_pin2, n74161_1_pin11, n74161_1_pin12, n74161_1_pin13, n74161_1_pin14,
       n74161_1_pin15, n74377_1_pin3, n74377_1_pin4, n74377_1_pin7, n74377_1_pin8, n74377_1_pin11,
       n74377_1_pin13, n74377_1_pin14, n74377_1_pin17, n74377_1_pin18, n74377_2_pin3, n74377_2_pin4,
       n74377_2_pin7, n74377_2_pin8, n74377_2_pin13, n74377_2_pin14, n74377_2_pin17, n74377_2_pin18,
       pull_resistor_1_node, pull_resistor_2_node, pull_resistor_3_node, pull_resistor_4_node;

  Pull_Resistor pull_resistor_1 (.node(pull_resistor_1_node));
  Pull_Resistor #(.pull(1)) pull_resistor_2 (.node(pull_resistor_2_node));
  _74377 u_74377_1 (
    .pin1(pull_resistor_1_node), .pin2(data[0]), .pin3(n74377_1_pin3), .pin4(n74377_1_pin4), .pin5(data[1]),
    .pin6(data[2]), .pin7(n74377_1_pin7), .pin8(n74377_1_pin8), .pin9(data[3]), .pin19(data[7]),
    .pin18(n74377_1_pin18), .pin17(n74377_1_pin17), .pin16(data[6]), .pin15(data[5]), .pin14(n74377_1_pin14),
    .pin13(n74377_1_pin13), .pin12(data[4]), .pin11(n74377_1_pin11));
  _74164 u_74164_1 (
    .pin1(pull_resistor_2_node), .pin2(serial), .pin3(n74377_1_pin3), .pin4(n74377_1_pin4),
    .pin5(n74377_1_pin7), .pin6(n74377_1_pin8), .pin13(n74377_1_pin18), .pin12(n74377_1_pin17),
    .pin11(n74377_1_pin14), .pin10(n74377_1_pin13), .pin9(pull_resistor_2_node), .pin8(clock));
  Pull_Resistor pull_resistor_3 (.node(pull_resistor_3_node));
  Pull_Resistor #(.pull(1)) pull_resistor_4 (.node(pull_resistor_4_node));
  _74161 u_74161_1 (
    .pin1(n74161_1_pin1), .pin2(n74161_1_pin2), .pin3(pull_resistor_3_node), .pin4(pull_resistor_3_node),
    .pin5(pull_resistor_3_node), .pin6(pull_resistor_3_node), .pin7(pull_resistor_4_node),
    .pin15(n74161_1_pin15), .pin14(n74161_1_pin14), .pin13(n74161_1_pin13), .pin12(n74161_1_pin12),
    .pin11(n74161_1_pin11), .pin10(pull_resistor_4_node), .pin9(pull_resistor_4_node));
  not not_1 (n74161_1_pin1, reset);
  not not_2 (n74161_1_pin2, clock);
  _74377 u_74377_2 (
    .pin1(pull_resistor_1_node), .pin2(data[8]), .pin3(n74377_2_pin3), .pin4(n74377_2_pin4), .pin5(data[9]),
    .pin6(data[10]), .pin7(n74377_2_pin7), .pin8(n74377_2_pin8), .pin9(data[11]), .pin19(data[15]),
    .pin18(n74377_2_pin18), .pin17(n74377_2_pin17), .pin16(data[14]), .pin15(data[13]),
    .pin14(n74377_2_pin14), .pin13(n74377_2_pin13), .pin12(data[12]), .pin11(n74377_1_pin11));
  _74164 u_74164_2 (
    .pin1(pull_resistor_2_node), .pin2(n74377_1_pin18), .pin3(n74377_2_pin3), .pin4(n74377_2_pin4),
    .pin5(n74377_2_pin7), .pin6(n74377_2_pin8), .pin13(n74377_2_pin18), .pin12(n74377_2_pin17),
    .pin11(n74377_2_pin14), .pin10(n74377_2_pin13), .pin9(pull_resistor_2_node), .pin8(clock));
  not not_3 (n74377_1_pin11, n74161_1_pin15);
  and and_1 (lb, n74161_1_pin14, n74161_1_pin13, n74161_1_pin12, n74161_1_pin11);
endmodule

module select_1_of_8 (
  input  s2,
  input  s1,
  input  s0,
  output out_4,
  output out_5,
  output out_6,
  output out_7,
  output out_8,
  output out_9,
  output out_10,
  output out_11
);

  wire not_1_out, not_2_out, not_3_out;

  not not_1 (not_1_out, s2);
  not not_2 (not_2_out, s1);
  not not_3 (not_3_out, s0);
  nor nor_1 (out_4, s0, s1, s2);
  nor nor_2 (out_5, not_3_out, s1, s2);
  nor nor_3 (out_6, s0, not_2_out, s2);
  nor nor_4 (out_7, not_3_out, not_2_out, s2);
  nor nor_5 (out_8, s0, s1, not_1_out);
  nor nor_6 (out_9, not_3_out, s1, not_1_out);
  nor nor_7 (out_10, s0, not_2_out, not_1_out);
  nor nor_8 (out_11, not_3_out, not_2_out, not_1_out);
endmodule

module select_1_of_16 (
  input  s3,
  input  s2,
  input  s1,
  input  s0,
  output out_5,
  output out_6,
  output out_7,
  output out_8,
  output out_9,
  output out_10,
  output out_11,
  output out_12,
  output out_13,
  output out_14,
  output out_15,
  output out_16,
  output out_17,
  output out_18,
  output out_19,
  output out_20
);

  wire not_1_out, not_2_out, not_3_out, not_4_out;

  not not_1 (not_1_out, s3);
  not not_2 (not_2_out, s2);
  not not_3 (not_3_out, s1);
  not not_4 (not_4_out, s0);
  nor nor_1 (out_5, s3, s2, s1, s0);
  nor nor_2 (out_6, s3, s2, s1, not_4_out);
  nor nor_3 (out_7, s3, s2, not_3_out, s0);
  nor nor_4 (out_8, s3, s2, not_3_out, not_4_out);
  nor nor_5 (out_9, s3, not_2_out, s1, s0);
  nor nor_6 (out_10, s3, not_2_out, s1, not_4_out);
  nor nor_7 (out_11, s3, not_2_out, not_3_out, s0);
  nor nor_8 (out_12, s3, not_2_out, not_3_out, not_4_out);
  nor nor_9 (out_13, not_1_out, s2, s1, s0);
  nor nor_10 (out_14, not_1_out, s2, s1, not_4_out);
  nor nor_11 (out_15, not_1_out, s2, not_3_out, s0);
  nor nor_12 (out_16, not_1_out, s2, not_3_out, not_4_out);
  nor nor_13 (out_17, not_1_out, not_2_out, s1, s0);
  nor nor_14 (out_18, not_1_out, not_2_out, s1, not_4_out);
  nor nor_15 (out_19, not_1_out, not_2_out, not_3_out, s0);
  nor nor_16 (out_20, not_1_out, not_2_out, not_3_out, not_4_out);
endmodule

module mux_16_to_8 (
  input  [7:0] d0,
  input  [7:0] d1,
  input  s,
  output [7:0] r
);

  wire not_1_out;

  not not_1 (not_1_out, s);
  and and_1 (r[0], d0[0], not_1_out);
  and and_2 (r[1], d0[1], not_1_out);
  and and_3 (r[2], d0[2], not_1_out);
  and and_4 (r[3], d0[3], not_1_out);
  and and_5 (r[4], d0[4], not_1_out);
  and and_6 (r[5], d0[5], not_1_out);
  and and_7 (r[6], d0[6], not_1_out);
  and and_8 (r[7], d0[7], not_1_out);
  and and_9 (r[0], d1[0], s);
  and and_10 (r[1], d1[1], s);
  and and_11 (r[2], d1[2], s);
  and and_12 (r[3], d1[3], s);
  and and_13 (r[4], d1[4], s);
  and and_14 (r[5], d1[5], s);
  and and_15 (r[6], d1[6], s);
  and and_16 (r[7], d1[7], s);
  Pull_Resistor pull_resistor_1 (.node(r[0]));
  Pull_Resistor pull_resistor_2 (.node(r[1]));
  Pull_Resistor pull_resistor_3 (.node(r[2]));
  Pull_Resistor pull_resistor_4 (.node(r[3]));
  Pull_Resistor pull_resistor_5 (.node(r[4]));
  Pull_Resistor pull_resistor_6 (.node(r[5]));
  Pull_Resistor pull_resistor_7 (.node(r[6]));
  Pull_Resistor pull_resistor_8 (.node(r[7]));

  // Notes on the sheet:
  //   and_1 drives only 1 and floats otherwise
  //   and_2 drives only 1 and floats otherwise
  //   and_3 drives only 1 and floats otherwise
  //   and_4 drives only 1 and floats otherwise
  //   and_5 drives only 1 and floats otherwise
  //   and_6 drives only 1 and floats otherwise
  //   and_7 drives only 1 and floats otherwise
  //   and_8 drives only 1 and floats otherwise
  //   and_9 drives only 1 and floats otherwise
  //   and_10 drives only 1 and floats otherwise
  //   and_11 drives only 1 and floats otherwise
  //   and_12 drives only 1 and floats otherwise
  //   and_13 drives only 1 and floats otherwise
  //   and_14 drives only 1 and floats otherwise
  //   and_15 drives only 1 and floats otherwise
  //   and_16 drives only 1 and floats otherwise
endmodule

module mux_32_to_16 (
  input  [15:0] d0,
  input  [15:0] d1,
  input  s,
  output [15:0] r
);

  wire not_1_out;

  assign r[0] = s ? d0[0] : 1'bz;  // Controlled_Buffer controlled_buffer_1
  assign r[0] = not_1_out ? d1[0] : 1'bz;  // Controlled_Buffer controlled_buffer_2
  assign r[1] = s ? d0[1] : 1'bz;  // Controlled_Buffer controlled_buffer_3
  assign r[1] = not_1_out ? d1[1] : 1'bz;  // Controlled_Buffer controlled_buffer_4
  assign r[2] = s ? d0[2] : 1'bz;  // Controlled_Buffer controlled_buffer_5
  assign r[2] = not_1_out ? d1[2] : 1'bz;  // Controlled_Buffer controlled_buffer_6
  assign r[3] = s ? d0[3] : 1'bz;  // Controlled_Buffer controlled_buffer_7
  assign r[3] = not_1_out ? d1[3] : 1'bz;  // Controlled_Buffer controlled_buffer_8
  assign r[4] = s ? d0[4] : 1'bz;  // Controlled_Buffer controlled_buffer_9
  assign r[4] = not_1_out ? d1[4] : 1'bz;  // Controlled_Buffer controlled_buffer_10
  assign r[5] = s ? d0[5] : 1'bz;  // Controlled_Buffer controlled_buffer_11
  assign r[5] = not_1_out ? d1[5] : 1'bz;  // Controlled_Buffer controlled_buffer_12
  assign r[6] = s ? d0[6] : 1'bz;  // Controlled_Buffer controlled_buffer_13
  assign r[6] = not_1_out ? d1[6] : 1'bz;  // Controlled_Buffer controlled_buffer_14
  assign r[7] = s ? d0[7] : 1'bz;  // Controlled_Buffer controlled_buffer_15
  assign r[7] = not_1_out ? d1[7] : 1'bz;  // Controlled_Buffer controlled_buffer_16
  assign r[8] = s ? d0[8] : 1'bz;  // Controlled_Buffer controlled_buffer_17
  assign r[8] = not_1_out ? d1[8] : 1'bz;  // Controlled_Buffer controlled_buffer_18
  assign r[9] = s ? d0[9] : 1'bz;  // Controlled_Buffer controlled_buffer_19
  assign r[9] = not_1_out ? d1[9] : 1'bz;  // Controlled_Buffer controlled_buffer_20
  assign r[10] = s ? d0[10] : 1'bz;  // Controlled_Buffer controlled_buffer_21
  assign r[10] = not_1_out ? d1[10] : 1'bz;  // Controlled_Buffer controlled_buffer_22
  assign r[11] = s ? d0[11] : 1'bz;  // Controlled_Buffer controlled_buffer_23
  assign r[11] = not_1_out ? d1[11] : 1'bz;  // Controlled_Buffer controlled_buffer_24
  assign r[12] = s ? d0[12] : 1'bz;  // Controlled_Buffer controlled_buffer_25
  assign r[12] = not_1_out ? d1[12] : 1'bz;  // Controlled_Buffer controlled_buffer_26
  assign r[13] = s ? d0[13] : 1'bz;  // Controlled_Buffer controlled_buffer_27
  assign r[13] = not_1_out ? d1[13] : 1'bz;  // Controlled_Buffer controlled_buffer_28
  assign r[14] = s ? d0[14] : 1'bz;  // Controlled_Buffer controlled_buffer_29
  assign r[14] = not_1_out ? d1[14] : 1'bz;  // Controlled_Buffer controlled_buffer_30
  assign r[15] = s ? d0[15] : 1'bz;  // Controlled_Buffer controlled_buffer_31
  assign r[15] = not_1_out ? d1[15] : 1'bz;  // Controlled_Buffer controlled_buffer_32
  not not_1 (not_1_out, s);
endmodule

module shift_right_8 (
  input  [7:0] a,
  output v,
  output [7:0] r
);


  assign r = {{2{a[7]}}, a[6:1]};
  assign v = a[0];
endmodule

module shift_left_8 (
  input  [7:0] a,
  output [7:0] r,
  output v
);


  assign r = {a[6:0], 1'b0};
  assign v = a[7];
endmodule

module zero_msb_8 (
  input  [7:0] a,
  output [7:0] r
);


  assign r = {1'b0, a[6:0]};
endmodule

module is_negative (
  input  [7:0] a,
  output r
);


  assign r = a[7];
endmodule

module is_zero (
  input  [7:0] a,
  output r
);

  nor nor_1 (r, a[0], a[1], a[2], a[3], a[4], a[5], a[6], a[7]);
endmodule

module hw_timer (
  input  reset,
  input  tick,
  input  active,
  input  switch,
  output [7:0] timestamp
);

  wire n74161_1_pin3, n74161_1_pin7, n74161_1_pin11, n74161_1_pin12, n74161_1_pin13, n74161_1_pin14,
       n74161_1_pin15, n74161_2_pin3, n74161_2_pin7, n74161_2_pin11, n74161_2_pin12, n74161_2_pin13,
       n74161_2_pin14, n74161_2_pin15, n74161_3_pin3, n74161_3_pin7, n74161_3_pin11, n74161_3_pin12,
       n74161_3_pin13, n74161_3_pin14, n74161_3_pin15, n74161_4_pin3, n74161_4_pin7, n74161_4_pin11,
       n74161_4_pin12, n74161_4_pin13, n74161_4_pin14, n74161_4_pin15, nor_1_out, nor_2_out, not_1_out,
       not_2_out, not_3_out, not_4_out, not_5_out, not_6_out;

  not not_1 (not_1_out, reset);
  _74161 u_74161_1 (
    .pin1(not_1_out), .pin2(tick), .pin3(n74161_1_pin3), .pin4(n74161_1_pin3), .pin5(n74161_1_pin3),
    .pin6(n74161_1_pin3), .pin7(n74161_1_pin7), .pin15(n74161_1_pin15), .pin14(n74161_1_pin14),
    .pin13(n74161_1_pin13), .pin12(n74161_1_pin12), .pin11(n74161_1_pin11), .pin10(n74161_1_pin7),
    .pin9(n74161_1_pin7));
  not not_2 (not_2_out, active);
  nor nor_1 (nor_1_out, not_2_out, not_3_out);
  not not_3 (not_3_out, switch);
  nor nor_2 (nor_2_out, not_2_out, switch);
  not not_4 (not_4_out, n74161_1_pin15);
  _74161 u_74161_2 (
    .pin1(not_1_out), .pin2(not_4_out), .pin3(n74161_2_pin3), .pin4(n74161_2_pin3), .pin5(n74161_2_pin3),
    .pin6(n74161_2_pin3), .pin7(n74161_2_pin7), .pin15(n74161_2_pin15), .pin14(n74161_2_pin14),
    .pin13(n74161_2_pin13), .pin12(n74161_2_pin12), .pin11(n74161_2_pin11), .pin10(n74161_2_pin7),
    .pin9(n74161_2_pin7));
  _74244 u_74244_1 (
    .pin1(nor_2_out), .pin2(n74161_1_pin14), .pin3(timestamp[0]), .pin4(n74161_1_pin13), .pin5(timestamp[1]),
    .pin6(n74161_1_pin12), .pin7(timestamp[2]), .pin8(n74161_1_pin11), .pin9(timestamp[3]),
    .pin19(nor_2_out), .pin18(timestamp[7]), .pin17(n74161_2_pin11), .pin16(timestamp[6]),
    .pin15(n74161_2_pin12), .pin14(timestamp[5]), .pin13(n74161_2_pin13), .pin12(timestamp[4]),
    .pin11(n74161_2_pin14));
  not not_5 (not_5_out, n74161_2_pin15);
  _74161 u_74161_3 (
    .pin1(not_1_out), .pin2(not_5_out), .pin3(n74161_3_pin3), .pin4(n74161_3_pin3), .pin5(n74161_3_pin3),
    .pin6(n74161_3_pin3), .pin7(n74161_3_pin7), .pin15(n74161_3_pin15), .pin14(n74161_3_pin14),
    .pin13(n74161_3_pin13), .pin12(n74161_3_pin12), .pin11(n74161_3_pin11), .pin10(n74161_3_pin7),
    .pin9(n74161_3_pin7));
  not not_6 (not_6_out, n74161_3_pin15);
  _74161 u_74161_4 (
    .pin1(not_1_out), .pin2(not_6_out), .pin3(n74161_4_pin3), .pin4(n74161_4_pin3), .pin5(n74161_4_pin3),
    .pin6(n74161_4_pin3), .pin7(n74161_4_pin7), .pin15(n74161_4_pin15), .pin14(n74161_4_pin14),
    .pin13(n74161_4_pin13), .pin12(n74161_4_pin12), .pin11(n74161_4_pin11), .pin10(n74161_4_pin7),
    .pin9(n74161_4_pin7));
  // NoConnect on n74161_4_pin15
  _74244 u_74244_2 (
    .pin1(nor_1_out), .pin2(n74161_3_pin14), .pin3(timestamp[7]), .pin4(n74161_3_pin13), .pin5(timestamp[6]),
    .pin6(n74161_3_pin12), .pin7(timestamp[5]), .pin8(n74161_3_pin11), .pin9(timestamp[4]),
    .pin19(nor_1_out), .pin18(timestamp[0]), .pin17(n74161_4_pin11), .pin16(timestamp[1]),
    .pin15(n74161_4_pin12), .pin14(timestamp[2]), .pin13(n74161_4_pin13), .pin12(timestamp[3]),
    .pin11(n74161_4_pin14));
  // also tied to GND on the sheet: {n74161_1_pin3, n74161_2_pin3, n74161_3_pin3, n74161_4_pin3}
  // also tied to VCC on the sheet: {n74161_1_pin7, n74161_2_pin7, n74161_3_pin7, n74161_4_pin7}

  // Notes on the sheet:
  //   low byte
  //   high byte
endmodule

module ic_tests (
  input  in_1,
  input  in_2,
  input  in_3,
  input  [7:0] in_4,
  input  [7:0] in_5,
  input  in_6,
  input  in_7,
  input  in_8,
  input  in_9
);

  wire and_1_out, and_2_out, and_3_out, and_4_out, and_5_out, and_6_out, and_7_out, and_8_out, n7402_1_pin2,
       n7402_1_pin3, n7402_1_pin5, n7402_1_pin6, n7402_1_pin8, n7402_1_pin9, n7402_1_pin11, n7402_1_pin12,
       n7402_2_pin2, n7402_2_pin3, n7402_2_pin5, n7402_2_pin6, n7402_2_pin8, n7402_2_pin9, n7402_2_pin11,
       n7402_2_pin12, n74161_1_pin3, n74161_1_pin7, n74161_1_pin11, n74161_1_pin12, n74161_1_pin13,
       n74161_1_pin14, n74161_1_pin15, n74240_1_pin3, n74240_1_pin5, n74240_1_pin7, n74240_1_pin9,
       n74240_1_pin12, n74240_1_pin14, n74240_1_pin16, n74240_1_pin18, n74240_2_pin1, n74240_2_pin2,
       n74240_2_pin3, n74240_2_pin4, n74240_2_pin5, n74240_2_pin6, n74240_2_pin7, n74240_2_pin8,
       n74240_2_pin9, n74240_2_pin11, n74240_2_pin12, n74240_2_pin13, n74240_2_pin14, n74240_2_pin15,
       n74240_2_pin16, n74240_2_pin17, n74240_2_pin18, n74244_1_pin3, n74244_1_pin5, n74244_1_pin7,
       n74244_1_pin9, n74244_1_pin12, n74244_1_pin14, n74244_1_pin16, n74244_1_pin18, n74377_1_pin11,
       n74377_2_pin2, n74377_2_pin5, n74377_2_pin6, n74377_2_pin9, n74377_2_pin14, n74377_2_pin17,
       n74377_2_pin18, n74377_2_pin19, not_1_out, not_2_out, not_3_out, not_4_out, not_5_out, not_6_out,
       not_7_out, not_8_out, not_9_out, not_10_out, not_11_out, not_12_out, not_13_out, not_14_out,
       not_15_out, not_16_out, not_17_out, not_18_out, not_19_out, not_20_out, not_21_out, not_22_out,
       not_23_out, not_24_out, not_25_out, or_1_out, or_2_out, or_3_out, or_4_out, or_5_out, or_6_out,
       or_7_out, or_8_out, pull_resistor_1_node, undriven;
  wire [7:0] n74377_1_pin9;

  not not_1 (not_1_out, undriven);
  _74377 u_74377_1 (
    .pin1(not_1_out), .pin2(n74377_1_pin9[5]), .pin3(in_4[4]), .pin4(in_4[5]), .pin5(n74377_1_pin9[6]),
    .pin6(n74377_1_pin9[7]), .pin7(in_4[6]), .pin8(in_4[7]), .pin9(n74377_1_pin9[0]),
    .pin19(n74377_1_pin9[4]), .pin18(in_4[3]), .pin17(in_4[2]), .pin16(n74377_1_pin9[3]),
    .pin15(n74377_1_pin9[2]), .pin14(in_4[1]), .pin13(in_4[0]), .pin12(n74377_1_pin9[1]),
    .pin11(n74377_1_pin11));
  and and_1 (and_1_out, in_8, in_9);
  not not_2 (not_2_out, in_8);
  or or_1 (or_1_out, not_2_out, not_3_out);
  not not_3 (not_3_out, in_9);
  and and_2 (and_2_out, in_8, not_4_out);
  not not_4 (not_4_out, in_9);
  not not_5 (not_5_out, in_8);
  or or_2 (or_2_out, not_5_out, in_9);
  not not_6 (not_6_out, or_1_out);
  not not_7 (not_7_out, or_2_out);
  and and_3 (and_3_out, in_8, in_9);
  not not_8 (not_8_out, in_8);
  or or_3 (or_3_out, not_8_out, not_9_out);
  not not_9 (not_9_out, in_9);
  and and_4 (and_4_out, in_8, not_10_out);
  not not_10 (not_10_out, in_9);
  not not_11 (not_11_out, in_8);
  or or_4 (or_4_out, not_11_out, in_9);
  _74161 u_74161_1 (
    .pin1(in_1), .pin2(in_2), .pin3(n74161_1_pin3), .pin4(n74161_1_pin3), .pin5(n74161_1_pin3),
    .pin6(n74161_1_pin3), .pin7(n74161_1_pin7), .pin15(n74161_1_pin15), .pin14(n74161_1_pin14),
    .pin13(n74161_1_pin13), .pin12(n74161_1_pin12), .pin11(n74161_1_pin11), .pin10(n74161_1_pin7),
    .pin9(n74161_1_pin7));
  // NoConnect on n74161_1_pin15
  not not_12 (not_12_out, and_3_out);
  not not_13 (not_13_out, and_4_out);
  not not_14 (not_14_out, in_8);
  and and_5 (and_5_out, not_14_out, not_15_out);
  not not_15 (not_15_out, in_9);
  or or_5 (or_5_out, in_8, in_9);
  not not_16 (not_16_out, in_8);
  and and_6 (and_6_out, not_16_out, in_9);
  or or_6 (or_6_out, in_8, not_17_out);
  not not_17 (not_17_out, in_9);
  _74240 u_74240_1 (
    .pin1(in_7), .pin2(in_5[4]), .pin3(n74240_1_pin3), .pin4(in_5[5]), .pin5(n74240_1_pin5), .pin6(in_5[6]),
    .pin7(n74240_1_pin7), .pin8(in_5[7]), .pin9(n74240_1_pin9), .pin19(in_7), .pin18(n74240_1_pin18),
    .pin17(in_5[3]), .pin16(n74240_1_pin16), .pin15(in_5[2]), .pin14(n74240_1_pin14), .pin13(in_5[1]),
    .pin12(n74240_1_pin12), .pin11(in_5[0]));
  not not_18 (not_18_out, and_5_out);
  not not_19 (not_19_out, and_6_out);
  not not_20 (not_20_out, in_8);
  and and_7 (and_7_out, not_20_out, not_21_out);
  not not_21 (not_21_out, in_9);
  or or_7 (or_7_out, in_8, in_9);
  not not_22 (not_22_out, in_8);
  and and_8 (and_8_out, not_22_out, in_9);
  or or_8 (or_8_out, in_8, not_23_out);
  not not_23 (not_23_out, in_9);
  not not_24 (not_24_out, or_7_out);
  not not_25 (not_25_out, or_8_out);
  _74244 u_74244_1 (
    .pin1(in_7), .pin2(in_5[4]), .pin3(n74244_1_pin3), .pin4(in_5[5]), .pin5(n74244_1_pin5), .pin6(in_5[6]),
    .pin7(n74244_1_pin7), .pin8(in_5[7]), .pin9(n74244_1_pin9), .pin19(in_7), .pin18(n74244_1_pin18),
    .pin17(in_5[3]), .pin16(n74244_1_pin16), .pin15(in_5[2]), .pin14(n74244_1_pin14), .pin13(in_5[1]),
    .pin12(n74244_1_pin12), .pin11(in_5[0]));
  _74240 u_74240_2 (
    .pin1(n74240_2_pin1), .pin2(n74240_2_pin2), .pin3(n74240_2_pin3), .pin4(n74240_2_pin4),
    .pin5(n74240_2_pin5), .pin6(n74240_2_pin6), .pin7(n74240_2_pin7), .pin8(n74240_2_pin8),
    .pin9(n74240_2_pin9), .pin19(n74240_2_pin1), .pin18(n74240_2_pin18), .pin17(n74240_2_pin17),
    .pin16(n74240_2_pin16), .pin15(n74240_2_pin15), .pin14(n74240_2_pin14), .pin13(n74240_2_pin13),
    .pin12(n74240_2_pin12), .pin11(n74240_2_pin11));
  _7402 u_7402_1 (
    .pin1(n74240_2_pin2), .pin2(n7402_1_pin2), .pin3(n7402_1_pin3), .pin4(n74240_2_pin4),
    .pin5(n7402_1_pin5), .pin6(n7402_1_pin6), .pin13(n74240_2_pin17), .pin12(n7402_1_pin12),
    .pin11(n7402_1_pin11), .pin10(n74240_2_pin15), .pin9(n7402_1_pin9), .pin8(n7402_1_pin8));
  _7402 u_7402_2 (
    .pin1(n74240_2_pin6), .pin2(n7402_2_pin2), .pin3(n7402_2_pin3), .pin4(n74240_2_pin8),
    .pin5(n7402_2_pin5), .pin6(n7402_2_pin6), .pin13(n74240_2_pin13), .pin12(n7402_2_pin12),
    .pin11(n7402_2_pin11), .pin10(n74240_2_pin11), .pin9(n7402_2_pin9), .pin8(n7402_2_pin8));
  Pull_Resistor pull_resistor_1 (.node(pull_resistor_1_node));
  _74377 u_74377_2 (
    .pin1(pull_resistor_1_node), .pin2(n74377_2_pin2), .pin3(in_3), .pin4(n74377_2_pin2),
    .pin5(n74377_2_pin5), .pin6(n74377_2_pin6), .pin7(n74377_2_pin5), .pin8(n74377_2_pin6),
    .pin9(n74377_2_pin9), .pin19(n74377_2_pin19), .pin18(n74377_2_pin18), .pin17(n74377_2_pin17),
    .pin16(n74377_2_pin18), .pin15(n74377_2_pin17), .pin14(n74377_2_pin14), .pin13(n74377_2_pin9),
    .pin12(n74377_2_pin14), .pin11(in_6));
  // also tied to GND on the sheet: n74161_1_pin3
  // also tied to VCC on the sheet: n74161_1_pin7

  // Notes on the sheet:
  //   74377 = Register
  //   3
  //   4
  //   4
  //   3
  //   74161 = Counter
  //   2
  //   5
  //   3
  //   4
  //   74240 = Inverter
  //   4
  //   3
  //   3
  //   4
  //   5
  //   2
  //   4
  //   3
  //   74244 = Buffer
endmodule
