// Logisim project computer.circ as structural Verilog: 15 circuits, main circuit Computer
module Computer (
  input  reset,
  input  timerClock,
  input  [7:0] in_3
);

  wire alu_1_carryflag, alu_1_negativeflag, alu_1_overflowflag, alu_1_zeroflag, and_1_out,
       conditionunit_1_inputreadyout, conditionunit_1_jumpresult, decoderunit_1_immediate,
       decoderunit_1_save, keyboarddriver_1_clock, keyboarddriver_1_serial, keyboarddriver_1_sync,
       n74138_1_pin7, n74138_1_pin9, n74138_1_pin10, n74138_1_pin11, n74138_1_pin12, n74138_1_pin13,
       n74138_1_pin14, n74138_1_pin15, not_1_out, not_2_out, or_1_out, pull_resistor_1_node,
       pull_resistor_2_node, pull_resistor_3_node, registerbank_1_inputready, registerbank_1_outputready,
       registerbank_1_soutclock, registerbank_1_soutdata, timer_out;
  wire [2:0] decoderunit_1_action, decoderunit_1_selector;
  wire [3:0] decoderunit_1_alu, decoderunit_1_jump;
  wire [7:0] alu_1_result, conditionunit_1_flags, decoderunit_1_byte, registerbank_1_operanda,
       registerbank_1_operandb;
  wire [15:0] dotmatrix_1_p1, dotmatrix_1_p2, programcounter_1_adr, registerbank_1_jumppointer, rom_1_data;

  Clock timer (.out(timer_out));
  and and_1 (and_1_out, n74138_1_pin13, timer_out);
  or or_1 (or_1_out, not_2_out, reset);
  ProgramCounter programcounter_1 (
    .pointer(registerbank_1_jumppointer), .jmp(conditionunit_1_jumpresult), .reset(or_1_out),
    .clock(and_1_out), .adr(programcounter_1_adr));
  ROM #(.addrWidth(16), .dataWidth(16)) rom_1 (.addr(programcounter_1_adr), .data(rom_1_data));
  DecoderUnit decoderunit_1 (
    .opcode(rom_1_data), .immediate(decoderunit_1_immediate), .action(decoderunit_1_action),
    .save(decoderunit_1_save), .\byte (decoderunit_1_byte), .selector(decoderunit_1_selector),
    .alu(decoderunit_1_alu), .jump(decoderunit_1_jump));
  KeyboardDriver keyboarddriver_1 (
    .keys(in_3), .ready(conditionunit_1_inputreadyout), .clockIN(and_1_out),
    .serial(keyboarddriver_1_serial), .clock(keyboarddriver_1_clock), .sync(keyboarddriver_1_sync));
  Pull_Resistor #(.pull(1)) pull_resistor_1 (.node(pull_resistor_1_node));
  _74138 u_74138_1 (
    .pin1(decoderunit_1_action[0]), .pin2(decoderunit_1_action[1]), .pin3(decoderunit_1_action[2]),
    .pin4(decoderunit_1_save), .pin5(decoderunit_1_save), .pin6(pull_resistor_1_node), .pin7(n74138_1_pin7),
    .pin15(n74138_1_pin15), .pin14(n74138_1_pin14), .pin13(n74138_1_pin13), .pin12(n74138_1_pin12),
    .pin11(n74138_1_pin11), .pin10(n74138_1_pin10), .pin9(n74138_1_pin9));
  RegisterBank registerbank_1 (
    .clock(and_1_out), .timerTick(timerClock), .reset(or_1_out), .sINdata(keyboarddriver_1_serial),
    .sINclock(keyboarddriver_1_clock), .sINsync(keyboarddriver_1_sync), .regSelect(decoderunit_1_selector),
    .status(conditionunit_1_flags), .saveMode(decoderunit_1_save), .aluResult(alu_1_result),
    .adrSave(decoderunit_1_action), .operandA(registerbank_1_operanda),
    .jumpPointer(registerbank_1_jumppointer), .sOutData(registerbank_1_soutdata),
    .sOutClock(registerbank_1_soutclock), .outputReady(registerbank_1_outputready),
    .operandB(registerbank_1_operandb), .inputReady(registerbank_1_inputready));
  // NoConnect on n74138_1_pin15
  not not_1 (not_1_out, n74138_1_pin14);
  not not_2 (not_2_out, n74138_1_pin12);
  // DotMatrix #(.dotshape("circle"), .inputtype("select"), .matrixcols(16), .matrixrows(16), .persist(48)) dotmatrix_1: pin names not known; wires that end beside it: dotmatrix_1_p1, dotmatrix_1_p2
  MatrixController_16p matrixcontroller_16p_1 (
    .serial(registerbank_1_soutdata), .clock(registerbank_1_soutclock), .reset(not_1_out),
    .anode(dotmatrix_1_p1), .kathode(dotmatrix_1_p2));
  Pull_Resistor pull_resistor_2 (.node(pull_resistor_2_node));
  Pull_Resistor pull_resistor_3 (.node(pull_resistor_3_node));
  ALU alu_1 (
    .instruction(decoderunit_1_alu), .A(registerbank_1_operanda), .B(registerbank_1_operandb),
    .immediateMode(decoderunit_1_immediate), .immediateValue(decoderunit_1_byte), .result(alu_1_result),
    .carryFlag(alu_1_carryflag), .negativeFlag(alu_1_negativeflag), .overflowFlag(alu_1_overflowflag),
    .zeroFlag(alu_1_zeroflag));
  ConditionUnit conditionunit_1 (
    .Negative(alu_1_negativeflag), .Zero(alu_1_zeroflag), .Carry(alu_1_carryflag),
    .Overflow(alu_1_overflowflag), .InputReady(registerbank_1_inputready),
    .OutputReady(registerbank_1_outputready), .in_8(pull_resistor_2_node), .in_9(pull_resistor_3_node),
    .clock(and_1_out), .instruction(decoderunit_1_jump), .InputReadyOut(conditionunit_1_inputreadyout),
    .Flags(conditionunit_1_flags), .jumpResult(conditionunit_1_jumpresult));

  // Notes on the sheet:
  //   Power On Reset
  //   NOP
  //   sync
  //   hold
  //   reset
  //   free actions
endmodule

module ALU (
  input  immediateMode,
  input  [3:0] instruction,
  input  [7:0] A,
  input  [7:0] B,
  input  [7:0] immediateValue,
  output [7:0] result,
  output zeroFlag,
  output carryFlag,
  output negativeFlag,
  output overflowFlag
);

  wire adder_1_cout, and_1_out, n7486_1_pin3, n7486_1_pin6, n7486_1_pin8, n7486_1_pin11, n7486_2_pin3,
       n7486_2_pin6, n7486_2_pin8, n7486_2_pin11, n7486_3_pin3, n7486_3_pin6, n7486_3_pin8, n74138_1_pin7,
       n74138_1_pin9, n74138_1_pin10, n74138_1_pin11, n74138_1_pin12, n74138_1_pin13, n74138_1_pin14,
       n74138_1_pin15, n74244_2_pin3, n74244_2_pin5, n74244_2_pin7, n74244_2_pin9, n74244_2_pin12,
       n74244_2_pin14, n74244_2_pin16, n74244_2_pin18, n74244_4_pin11, n74244_8_pin3, n74244_8_pin5,
       n74244_8_pin7, n74244_8_pin9, n74244_8_pin12, n74244_8_pin14, n74244_8_pin16, n74244_8_pin18,
       nand_1_out, nand_2_out, nand_3_out, nand_4_out, nand_5_out, nand_6_out, nand_7_out, nand_8_out,
       nand_9_out, nand_10_out, nor_1_out, nor_2_out, nor_3_out, nor_4_out, nor_5_out, nor_6_out, nor_7_out,
       nor_8_out, not_1_out, not_2_out, not_3_out, not_4_out, not_5_out, not_6_out, not_7_out,
       pull_resistor_1_node, xor_1_out;
  wire [6:0] adder_1_out;
  wire [7:0] n74244_9_pin9;

  // Probe on result
  Pull_Resistor #(.pull(1)) pull_resistor_1 (.node(pull_resistor_1_node));
  not not_1 (not_1_out, immediateMode);
  nor nor_1 (nor_1_out, A[0], B[0]);
  nor nor_2 (nor_2_out, A[1], B[1]);
  nor nor_3 (nor_3_out, A[2], B[2]);
  nor nor_4 (nor_4_out, A[3], B[3]);
  nor nor_5 (nor_5_out, A[4], B[4]);
  nor nor_6 (nor_6_out, A[5], B[5]);
  nor nor_7 (nor_7_out, A[6], B[6]);
  nor nor_8 (nor_8_out, A[7], B[7]);
  nand nand_1 (nand_1_out, instruction[3], not_2_out);
  not not_2 (not_2_out, instruction[2]);
  _74138 u_74138_1 (
    .pin1(instruction[0]), .pin2(instruction[1]), .pin3(instruction[2]), .pin4(instruction[3]),
    .pin5(immediateMode), .pin6(pull_resistor_1_node), .pin7(n74138_1_pin7), .pin15(n74138_1_pin15),
    .pin14(n74138_1_pin14), .pin13(n74138_1_pin13), .pin12(n74138_1_pin12), .pin11(n74138_1_pin11),
    .pin10(n74138_1_pin10), .pin9(n74138_1_pin9));
  _74240 u_74240_1 (
    .pin1(n74138_1_pin10), .pin2(nor_5_out), .pin3(result[3]), .pin4(nor_6_out), .pin5(result[2]),
    .pin6(nor_7_out), .pin7(result[1]), .pin8(nor_8_out), .pin9(result[0]), .pin19(n74138_1_pin10),
    .pin18(result[4]), .pin17(nor_4_out), .pin16(result[5]), .pin15(nor_3_out), .pin14(result[6]),
    .pin13(nor_2_out), .pin12(result[7]), .pin11(nor_1_out));
  and and_1 (and_1_out, n74138_1_pin9, n74138_1_pin7);
  nand nand_2 (nand_2_out, A[0], B[0]);
  nand nand_3 (nand_3_out, A[1], B[1]);
  nand nand_4 (nand_4_out, A[2], B[2]);
  nand nand_5 (nand_5_out, A[3], B[3]);
  nand nand_6 (nand_6_out, A[4], B[4]);
  nand nand_7 (nand_7_out, A[5], B[5]);
  nand nand_8 (nand_8_out, A[6], B[6]);
  nand nand_9 (nand_9_out, A[7], B[7]);
  _74240 u_74240_2 (
    .pin1(n74138_1_pin11), .pin2(nand_6_out), .pin3(result[3]), .pin4(nand_7_out), .pin5(result[2]),
    .pin6(nand_8_out), .pin7(result[1]), .pin8(nand_9_out), .pin9(result[0]), .pin19(n74138_1_pin11),
    .pin18(result[4]), .pin17(nand_5_out), .pin16(result[5]), .pin15(nand_4_out), .pin14(result[6]),
    .pin13(nand_3_out), .pin12(result[7]), .pin11(nand_2_out));
  _74244 u_74244_1 (
    .pin1(not_1_out), .pin2(immediateValue[3]), .pin3(result[3]), .pin4(immediateValue[4]), .pin5(result[2]),
    .pin6(immediateValue[5]), .pin7(result[1]), .pin8(immediateValue[6]), .pin9(result[0]),
    .pin19(not_1_out), .pin18(result[4]), .pin17(immediateValue[2]), .pin16(result[5]),
    .pin15(immediateValue[1]), .pin14(result[6]), .pin13(immediateValue[0]), .pin12(result[7]),
    .pin11(immediateValue[7]));
  Pull_Resistor #(.pull(1)) pull_resistor_2 (.node(result[7]));
  Pull_Resistor #(.pull(1)) pull_resistor_3 (.node(result[6]));
  _74244 u_74244_2 (
    .pin1(instruction[0]), .pin2(B[7]), .pin3(n74244_2_pin3), .pin4(B[6]), .pin5(n74244_2_pin5), .pin6(B[1]),
    .pin7(n74244_2_pin7), .pin8(B[0]), .pin9(n74244_2_pin9), .pin19(instruction[0]), .pin18(n74244_2_pin18),
    .pin17(B[2]), .pin16(n74244_2_pin16), .pin15(B[3]), .pin14(n74244_2_pin14), .pin13(B[4]),
    .pin12(n74244_2_pin12), .pin11(B[5]));
  Pull_Resistor #(.pull(1)) pull_resistor_4 (.node(result[5]));
  Pull_Resistor #(.pull(1)) pull_resistor_5 (.node(result[4]));
  Pull_Resistor #(.pull(1)) pull_resistor_6 (.node(result[3]));
  Pull_Resistor #(.pull(1)) pull_resistor_7 (.node(result[2]));
  Pull_Resistor #(.pull(1)) pull_resistor_8 (.node(n74244_2_pin18));
  Pull_Resistor #(.pull(1)) pull_resistor_9 (.node(n74244_2_pin16));
  Pull_Resistor #(.pull(1)) pull_resistor_10 (.node(n74244_2_pin14));
  Pull_Resistor #(.pull(1)) pull_resistor_11 (.node(n74244_2_pin12));
  Pull_Resistor #(.pull(1)) pull_resistor_12 (.node(n74244_2_pin9));
  Pull_Resistor #(.pull(1)) pull_resistor_13 (.node(n74244_2_pin7));
  Pull_Resistor #(.pull(1)) pull_resistor_14 (.node(n74244_2_pin5));
  Pull_Resistor #(.pull(1)) pull_resistor_15 (.node(n74244_2_pin3));
  Pull_Resistor #(.pull(1)) pull_resistor_16 (.node(result[1]));
  Pull_Resistor #(.pull(1)) pull_resistor_17 (.node(result[0]));
  _7486 u_7486_1 (
    .pin1(A[7]), .pin2(n74244_2_pin18), .pin3(n7486_1_pin3), .pin4(n74244_2_pin16), .pin5(A[6]),
    .pin6(n7486_1_pin6), .pin13(A[0]), .pin12(n74244_2_pin12), .pin11(n7486_1_pin11), .pin10(n74244_2_pin14),
    .pin9(A[1]), .pin8(n7486_1_pin8));
  _7486 u_7486_2 (
    .pin1(A[5]), .pin2(n74244_2_pin9), .pin3(n7486_2_pin3), .pin4(n74244_2_pin7), .pin5(A[4]),
    .pin6(n7486_2_pin6), .pin13(A[2]), .pin12(n74244_2_pin3), .pin11(n7486_2_pin11), .pin10(n74244_2_pin5),
    .pin9(A[3]), .pin8(n7486_2_pin8));
  _74244 u_74244_3 (
    .pin1(and_1_out), .pin2(n7486_2_pin6), .pin3(result[3]), .pin4(n7486_2_pin3), .pin5(result[2]),
    .pin6(n7486_1_pin6), .pin7(result[1]), .pin8(n7486_1_pin3), .pin9(result[0]), .pin19(and_1_out),
    .pin18(result[4]), .pin17(n7486_2_pin8), .pin16(result[5]), .pin15(n7486_2_pin11), .pin14(result[6]),
    .pin13(n7486_1_pin8), .pin12(result[7]), .pin11(n7486_1_pin11));
  not not_3 (not_3_out, n74138_1_pin12);
  nand nand_10 (nand_10_out, not_3_out, A[7]);
  _74244 u_74244_4 (
    .pin1(n74138_1_pin12), .pin2(A[3]), .pin3(result[3]), .pin4(A[4]), .pin5(result[2]), .pin6(A[5]),
    .pin7(result[1]), .pin8(A[6]), .pin9(result[0]), .pin19(n74138_1_pin12), .pin18(result[4]), .pin17(A[2]),
    .pin16(result[5]), .pin15(A[1]), .pin14(result[6]), .pin13(A[0]), .pin12(result[7]),
    .pin11(n74244_4_pin11));
  Pull_Resistor pull_resistor_18 (.node(n74244_4_pin11));
  not not_4 (not_4_out, n74138_1_pin13);
  nand nand_11 (nand_10_out, not_4_out, A[0]);
  _74244 u_74244_5 (
    .pin1(n74138_1_pin13), .pin2(A[5]), .pin3(result[3]), .pin4(A[6]), .pin5(result[2]), .pin6(A[7]),
    .pin7(result[1]), .pin8(A[7]), .pin9(result[0]), .pin19(n74138_1_pin13), .pin18(result[4]), .pin17(A[4]),
    .pin16(result[5]), .pin15(A[3]), .pin14(result[6]), .pin13(A[2]), .pin12(result[7]), .pin11(A[1]));
  _74244 u_74244_6 (
    .pin1(n74138_1_pin15), .pin2(A[4]), .pin3(result[3]), .pin4(A[5]), .pin5(result[2]), .pin6(A[6]),
    .pin7(result[1]), .pin8(A[7]), .pin9(result[0]), .pin19(n74138_1_pin15), .pin18(result[4]), .pin17(A[3]),
    .pin16(result[5]), .pin15(A[2]), .pin14(result[6]), .pin13(A[1]), .pin12(result[7]), .pin11(A[0]));
  _74244 u_74244_7 (
    .pin1(n74138_1_pin14), .pin2(B[4]), .pin3(result[3]), .pin4(B[5]), .pin5(result[2]), .pin6(B[6]),
    .pin7(result[1]), .pin8(B[7]), .pin9(result[0]), .pin19(n74138_1_pin14), .pin18(result[4]), .pin17(B[3]),
    .pin16(result[5]), .pin15(B[2]), .pin14(result[6]), .pin13(B[1]), .pin12(result[7]), .pin11(B[0]));
  _74244 u_74244_8 (
    .pin1(instruction[0]), .pin2(B[0]), .pin3(n74244_8_pin3), .pin4(B[1]), .pin5(n74244_8_pin5), .pin6(B[2]),
    .pin7(n74244_8_pin7), .pin8(B[3]), .pin9(n74244_8_pin9), .pin19(instruction[0]), .pin18(n74244_8_pin18),
    .pin17(B[7]), .pin16(n74244_8_pin16), .pin15(B[6]), .pin14(n74244_8_pin14), .pin13(B[5]),
    .pin12(n74244_8_pin12), .pin11(B[4]));
  _74244 u_74244_9 (
    .pin1(instruction[1]), .pin2(n74244_8_pin9), .pin3(n74244_9_pin9[3]), .pin4(n74244_8_pin7),
    .pin5(n74244_9_pin9[2]), .pin6(n74244_8_pin5), .pin7(n74244_9_pin9[1]), .pin8(n74244_8_pin3),
    .pin9(n74244_9_pin9[0]), .pin19(instruction[1]), .pin18(n74244_9_pin9[4]), .pin17(n74244_8_pin12),
    .pin16(n74244_9_pin9[5]), .pin15(n74244_8_pin14), .pin14(n74244_9_pin9[6]), .pin13(n74244_8_pin16),
    .pin12(n74244_9_pin9[7]), .pin11(n74244_8_pin18));
  Pull_Resistor #(.pull(1)) pull_resistor_19 (.node(n74244_8_pin18));
  Pull_Resistor pull_resistor_20 (.node(n74244_8_pin16));
  Pull_Resistor pull_resistor_21 (.node(n74244_8_pin14));
  Pull_Resistor pull_resistor_22 (.node(n74244_8_pin12));
  not not_5 (not_5_out, instruction[1]);
  _74240 u_74240_3 (
    .pin1(not_5_out), .pin2(n74244_8_pin9), .pin3(n74244_9_pin9[3]), .pin4(n74244_8_pin7),
    .pin5(n74244_9_pin9[2]), .pin6(n74244_8_pin5), .pin7(n74244_9_pin9[1]), .pin8(n74244_8_pin3),
    .pin9(n74244_9_pin9[0]), .pin19(not_5_out), .pin18(n74244_9_pin9[4]), .pin17(n74244_8_pin12),
    .pin16(n74244_9_pin9[5]), .pin15(n74244_8_pin14), .pin14(n74244_9_pin9[6]), .pin13(n74244_8_pin16),
    .pin12(n74244_9_pin9[7]), .pin11(n74244_8_pin18));
  Pull_Resistor pull_resistor_23 (.node(n74244_8_pin9));
  Pull_Resistor pull_resistor_24 (.node(n74244_8_pin7));
  Pull_Resistor pull_resistor_25 (.node(n74244_8_pin5));
  Pull_Resistor pull_resistor_26 (.node(n74244_8_pin3));
  not not_6 (not_6_out, not_5_out);
  _7486 u_7486_3 (
    .pin1(instruction[1]), .pin2(A[7]), .pin3(n7486_3_pin3), .pin4(n7486_3_pin3), .pin5(B[7]),
    .pin6(n7486_3_pin6), .pin10(B[7]), .pin9(negativeFlag), .pin8(n7486_3_pin8));  // open: pin13, pin12, pin11
  Adder adder_1 (.a(A), .b(n74244_9_pin9), .out({negativeFlag, adder_1_out}), .cin(not_6_out), .cout(adder_1_cout));
  xor xor_1 (xor_1_out, adder_1_cout, not_6_out);
  assign nand_10_out = not_7_out ? ~xor_1_out : 1'bz;  // Controlled_Inverter controlled_inverter_1
  Pull_Resistor #(.pull(1)) pull_resistor_27 (.node(nand_10_out));
  not not_7 (not_7_out, nand_1_out);
  not not_8 (carryFlag, nand_10_out);
  _74244 u_74244_10 (
    .pin1(nand_1_out), .pin2(adder_1_out[4]), .pin3(result[3]), .pin4(adder_1_out[5]), .pin5(result[2]),
    .pin6(adder_1_out[6]), .pin7(result[1]), .pin8(negativeFlag), .pin9(result[0]), .pin19(nand_1_out),
    .pin18(result[4]), .pin17(adder_1_out[3]), .pin16(result[5]), .pin15(adder_1_out[2]), .pin14(result[6]),
    .pin13(adder_1_out[1]), .pin12(result[7]), .pin11(adder_1_out[0]));
  nand nand_12 (overflowFlag, n7486_3_pin8, n7486_3_pin6);
  nor nor_9 (zeroFlag, result[0], result[1], result[2], result[3], result[4], result[5], result[6], result[7]);

  // Notes on the sheet:
  //   result
  //   transistoren für nors
  //   enable output for adder
  //   0: =A
  //   1: =B
  //   2: ASHR
  //   3: ASHL
  //   4: AND
  //   5: OR
  //   6: XOR
  //   7: NOT
  //   OR
  //   AND
  //   ashr
  //   ashl
  //   xor / inv
  //   transistoren für nands
  //   7
  //   6
  //   1
  //   0
  //   xor / inv
  //   XOR / INV
  //   2
  //   3
  //   4
  //   5
  //   increase / decrease
  //   xor
  //   xor
  //   xor / inv
  //   ashl
  //   ashr
  //   nand_10 drives only 0 and floats otherwise
  //   carry
  //   tri-state
  //   ashl
  //   nand_11 drives only 0 and floats otherwise
  //   subtraction
  //   ashr
  //   take A
  //   take B
  //   Y (add)
  //   Y / 01
  //   0
  //   1
  //   2
  //   3
  //   !Y (sub)
  //   4
  //   5
  //   6
  //   7
  //   msb B
  //   subtract
  //   msb A
  //   msb R
  //   8 bit adder
endmodule

module DecoderUnit (
  input  [15:0] opcode,
  output [2:0] selector,
  output [3:0] alu,
  output [7:0] \byte ,
  output immediate,
  output [2:0] action,
  output save,
  output [3:0] jump
);


  assign action = opcode[11:9];
  assign alu = opcode[6:3];
  assign \byte  = opcode[7:0];
  assign immediate = opcode[8];
  assign jump = {opcode[7], opcode[15:13]};
  assign save = opcode[12];
  assign selector = opcode[2:0];

  // Notes on the sheet:
  //   splits the instruction into all commands
endmodule

module ConditionUnit (
  input  [3:0] instruction,
  input  Negative,
  input  Zero,
  input  Carry,
  input  Overflow,
  input  InputReady,
  input  OutputReady,
  input  in_8,
  input  in_9,
  input  clock,
  output jumpResult,
  output InputReadyOut,
  output [7:0] Flags
);

  wire not_1_out, not_2_out, not_3_out, pull_resistor_1_node;

  _74377 u_74377_1 (
    .pin1(instruction[3]), .pin2(Flags[5]), .pin3(InputReady), .pin4(OutputReady), .pin5(Flags[6]),
    .pin6(Flags[7]), .pin7(in_8), .pin8(in_9), .pin9(Flags[0]), .pin19(Flags[4]), .pin18(Overflow),
    .pin17(Carry), .pin16(Flags[3]), .pin15(Flags[2]), .pin14(Zero), .pin13(Negative), .pin12(Flags[1]),
    .pin11(clock));
  not not_1 (not_1_out, instruction[1]);
  not not_2 (not_2_out, instruction[0]);
  _7410 u_7410_1 ();  // open: pin1, pin2, pin3, pin4, pin5, pin6, pin13, pin12, pin11, pin10, pin9, pin8
  xor xor_1 (jumpResult, instruction[2], not_3_out);
  not not_3 (not_3_out, pull_resistor_1_node);
  Pull_Resistor #(.pull(1)) pull_resistor_1 (.node(pull_resistor_1_node));
  nand nand_1 (pull_resistor_1_node, instruction[1], instruction[0], Flags[3]);
  nand nand_2 (pull_resistor_1_node, instruction[1], not_2_out, Flags[2]);
  nand nand_3 (pull_resistor_1_node, instruction[0], not_1_out, Flags[1]);

  assign InputReadyOut = Flags[5];

  // Notes on the sheet:
  //   nand_1 drives only 0 and floats otherwise
  //   nand_2 drives only 0 and floats otherwise
  //   nand_3 drives only 0 and floats otherwise
endmodule

module ProgramCounter (
  input  [15:0] pointer,
  input  jmp,
  input  reset,
  input  clock,
  output [15:0] adr
);

  wire n74161_1_pin7, n74161_1_pin15, n74161_2_pin7, n74161_2_pin15, n74161_3_pin7, n74161_3_pin15,
       n74161_4_pin7, not_1_out, not_2_out, not_3_out;

  not not_1 (not_1_out, jmp);
  not not_2 (not_2_out, reset);
  not not_3 (not_3_out, clock);
  _74161 u_74161_1 (
    .pin1(not_2_out), .pin2(not_3_out), .pin3(pointer[0]), .pin4(pointer[1]), .pin5(pointer[2]),
    .pin6(pointer[3]), .pin7(n74161_1_pin7), .pin15(n74161_1_pin15), .pin14(adr[0]), .pin13(adr[1]),
    .pin12(adr[2]), .pin11(adr[3]), .pin10(n74161_1_pin7), .pin9(not_1_out));
  _74161 u_74161_2 (
    .pin1(not_2_out), .pin2(not_3_out), .pin3(pointer[4]), .pin4(pointer[5]), .pin5(pointer[6]),
    .pin6(pointer[7]), .pin7(n74161_2_pin7), .pin15(n74161_2_pin15), .pin14(adr[4]), .pin13(adr[5]),
    .pin12(adr[6]), .pin11(adr[7]), .pin10(n74161_1_pin15), .pin9(not_1_out));
  _74161 u_74161_3 (
    .pin1(not_2_out), .pin2(not_3_out), .pin3(pointer[8]), .pin4(pointer[9]), .pin5(pointer[10]),
    .pin6(pointer[11]), .pin7(n74161_3_pin7), .pin15(n74161_3_pin15), .pin14(adr[8]), .pin13(adr[9]),
    .pin12(adr[10]), .pin11(adr[11]), .pin10(n74161_2_pin15), .pin9(not_1_out));
  _74161 u_74161_4 (
    .pin1(not_2_out), .pin2(not_3_out), .pin3(pointer[12]), .pin4(pointer[13]), .pin5(pointer[14]),
    .pin6(pointer[15]), .pin7(n74161_4_pin7), .pin14(adr[12]), .pin13(adr[13]), .pin12(adr[14]),
    .pin11(adr[15]), .pin10(n74161_3_pin15), .pin9(not_1_out));  // open: pin15
  // also tied to VCC on the sheet: {n74161_1_pin7, n74161_2_pin7, n74161_3_pin7, n74161_4_pin7}

  // Notes on the sheet:
  //   pointer: initial=0x2a
endmodule

module RegisterBank (
  input  [2:0] adrSave,
  input  clock,
  input  saveMode,
  input  [7:0] aluResult,
  input  [2:0] regSelect,
  input  [7:0] status,
  input  sINdata,
  input  sINclock,
  input  sINsync,
  input  timerTick,
  input  reset,
  output [7:0] operandA,
  output sOutData,
  output sOutClock,
  output outputReady,
  output [7:0] operandB,
  output [15:0] jumpPointer,
  output inputReady
);

  wire and_1_out, buffer_1_out, buffer_2_out, buffer_3_out, buffer_4_out, buffer_5_out, buffer_6_out,
       deserialise_8_1_fb, n74138_1_pin4, n74138_1_pin7, n74138_1_pin9, n74138_1_pin10, n74138_1_pin11,
       n74138_1_pin12, n74138_1_pin13, n74138_1_pin14, n74138_1_pin15, n74138_2_pin4, n74138_2_pin6,
       n74138_2_pin7, n74138_2_pin9, n74138_2_pin10, n74138_2_pin11, n74138_2_pin12, n74138_2_pin13,
       n74138_2_pin14, n74138_2_pin15, nor_1_out, nor_2_out, nor_4_out, nor_5_out, not_1_out, not_2_out,
       not_3_out, not_4_out, not_5_out, not_6_out, not_7_out, not_8_out, not_9_out, not_10_out, not_11_out,
       not_12_out, not_13_out;
  wire [7:0] deserialise_8_1_data, n74377_4_pin9, n74377_5_pin9, n74377_6_pin9;

  _74138 u_74138_1 (
    .pin1(adrSave[0]), .pin2(adrSave[1]), .pin3(adrSave[2]), .pin4(n74138_1_pin4), .pin5(n74138_1_pin4),
    .pin6(saveMode), .pin7(n74138_1_pin7), .pin15(n74138_1_pin15), .pin14(n74138_1_pin14),
    .pin13(n74138_1_pin13), .pin12(n74138_1_pin12), .pin11(n74138_1_pin11), .pin10(n74138_1_pin10),
    .pin9(n74138_1_pin9));
  Pull_Resistor pull_resistor_1 (.node(n74138_1_pin4));
  _74377 u_74377_1 (
    .pin1(n74138_1_pin15), .pin2(operandA[5]), .pin3(aluResult[4]), .pin4(aluResult[5]), .pin5(operandA[6]),
    .pin6(operandA[7]), .pin7(aluResult[6]), .pin8(aluResult[7]), .pin9(operandA[0]), .pin19(operandA[4]),
    .pin18(aluResult[3]), .pin17(aluResult[2]), .pin16(operandA[3]), .pin15(operandA[2]),
    .pin14(aluResult[1]), .pin13(aluResult[0]), .pin12(operandA[1]), .pin11(clock));
  _74377 u_74377_2 (
    .pin1(n74138_1_pin14), .pin2(jumpPointer[5]), .pin3(aluResult[4]), .pin4(aluResult[5]),
    .pin5(jumpPointer[6]), .pin6(jumpPointer[7]), .pin7(aluResult[6]), .pin8(aluResult[7]),
    .pin9(jumpPointer[0]), .pin19(jumpPointer[4]), .pin18(aluResult[3]), .pin17(aluResult[2]),
    .pin16(jumpPointer[3]), .pin15(jumpPointer[2]), .pin14(aluResult[1]), .pin13(aluResult[0]),
    .pin12(jumpPointer[1]), .pin11(clock));
  _74377 u_74377_3 (
    .pin1(n74138_1_pin13), .pin2(jumpPointer[13]), .pin3(aluResult[4]), .pin4(aluResult[5]),
    .pin5(jumpPointer[14]), .pin6(jumpPointer[15]), .pin7(aluResult[6]), .pin8(aluResult[7]),
    .pin9(jumpPointer[8]), .pin19(jumpPointer[12]), .pin18(aluResult[3]), .pin17(aluResult[2]),
    .pin16(jumpPointer[11]), .pin15(jumpPointer[10]), .pin14(aluResult[1]), .pin13(aluResult[0]),
    .pin12(jumpPointer[9]), .pin11(clock));
  _74377 u_74377_4 (
    .pin1(n74138_1_pin11), .pin2(n74377_4_pin9[5]), .pin3(aluResult[4]), .pin4(aluResult[5]),
    .pin5(n74377_4_pin9[6]), .pin6(n74377_4_pin9[7]), .pin7(aluResult[6]), .pin8(aluResult[7]),
    .pin9(n74377_4_pin9[0]), .pin19(n74377_4_pin9[4]), .pin18(aluResult[3]), .pin17(aluResult[2]),
    .pin16(n74377_4_pin9[3]), .pin15(n74377_4_pin9[2]), .pin14(aluResult[1]), .pin13(aluResult[0]),
    .pin12(n74377_4_pin9[1]), .pin11(clock));
  _74377 u_74377_5 (
    .pin1(n74138_1_pin10), .pin2(n74377_5_pin9[5]), .pin3(aluResult[4]), .pin4(aluResult[5]),
    .pin5(n74377_5_pin9[6]), .pin6(n74377_5_pin9[7]), .pin7(aluResult[6]), .pin8(aluResult[7]),
    .pin9(n74377_5_pin9[0]), .pin19(n74377_5_pin9[4]), .pin18(aluResult[3]), .pin17(aluResult[2]),
    .pin16(n74377_5_pin9[3]), .pin15(n74377_5_pin9[2]), .pin14(aluResult[1]), .pin13(aluResult[0]),
    .pin12(n74377_5_pin9[1]), .pin11(clock));
  _74377 u_74377_6 (
    .pin1(n74138_1_pin9), .pin2(n74377_6_pin9[5]), .pin3(aluResult[4]), .pin4(aluResult[5]),
    .pin5(n74377_6_pin9[6]), .pin6(n74377_6_pin9[7]), .pin7(aluResult[6]), .pin8(aluResult[7]),
    .pin9(n74377_6_pin9[0]), .pin19(n74377_6_pin9[4]), .pin18(aluResult[3]), .pin17(aluResult[2]),
    .pin16(n74377_6_pin9[3]), .pin15(n74377_6_pin9[2]), .pin14(aluResult[1]), .pin13(aluResult[0]),
    .pin12(n74377_6_pin9[1]), .pin11(clock));
  not not_1 (not_1_out, n74138_1_pin7);
  serialise_8 serialise_8_1 (
    .clock(clock), .start(not_1_out), .data(aluResult), .serial(sOutData), .tick(sOutClock),
    .outputReady(outputReady));
  not not_2 (not_2_out, n74138_1_pin12);
  synced_RAM synced_ram_1 (
    .writeEnable(not_2_out), .clock(clock), .outputEnable(not_7_out), .busIN(aluResult),
    .adress(jumpPointer[12:0]), .busOUT(operandB));
  and and_1 (and_1_out, jumpPointer[13], not_8_out);
  hw_timer hw_timer_1 (
    .reset(reset), .tick(timerTick), .active(and_1_out), .switch(jumpPointer[14]), .timestamp(operandB));
  not not_3 (not_3_out, not_8_out);
  Pull_Resistor pull_resistor_2 (.node(operandB));
  nor nor_1 (nor_1_out, not_3_out, jumpPointer[13], jumpPointer[14]);
  deserialise_8 deserialise_8_1 (
    .serial(sINdata), .clock(sINclock), .reset(sINsync), .fb(deserialise_8_1_fb), .data(deserialise_8_1_data));
  assign operandB = nor_1_out ? deserialise_8_1_data : 8'bz;  // Controlled_Buffer controlled_buffer_1
  _74138 u_74138_2 (
    .pin1(regSelect[0]), .pin2(regSelect[1]), .pin3(regSelect[2]), .pin4(n74138_2_pin4),
    .pin5(n74138_2_pin4), .pin6(n74138_2_pin6), .pin7(n74138_2_pin7), .pin15(n74138_2_pin15),
    .pin14(n74138_2_pin14), .pin13(n74138_2_pin13), .pin12(n74138_2_pin12), .pin11(n74138_2_pin11),
    .pin10(n74138_2_pin10), .pin9(n74138_2_pin9));
  Pull_Resistor pull_resistor_3 (.node(n74138_2_pin4));
  Pull_Resistor #(.pull(1)) pull_resistor_4 (.node(n74138_2_pin6));
  not not_4 (not_4_out, n74138_2_pin15);
  not not_5 (not_5_out, n74138_2_pin14);
  not not_6 (not_6_out, n74138_2_pin13);
  not not_7 (not_7_out, n74138_2_pin12);
  not not_8 (not_8_out, n74138_2_pin11);
  not not_9 (not_9_out, n74138_2_pin10);
  not not_10 (not_10_out, n74138_2_pin9);
  not not_11 (not_11_out, n74138_2_pin7);
  assign operandB = not_9_out ? n74377_5_pin9 : 8'bz;  // Controlled_Buffer controlled_buffer_2
  assign operandB = not_10_out ? n74377_6_pin9 : 8'bz;  // Controlled_Buffer controlled_buffer_3
  assign operandB = not_11_out ? status : 8'bz;  // Controlled_Buffer controlled_buffer_4
  buf buffer_1 (buffer_1_out, nor_1_out);
  buf buffer_2 (buffer_2_out, buffer_1_out);
  buf buffer_3 (buffer_3_out, buffer_2_out);
  not not_12 (not_12_out, nor_1_out);
  buf buffer_4 (buffer_4_out, deserialise_8_1_fb);
  buf buffer_5 (buffer_5_out, buffer_4_out);
  buf buffer_6 (buffer_6_out, buffer_5_out);
  not not_13 (not_13_out, deserialise_8_1_fb);
  assign operandB = not_4_out ? n74377_4_pin9 : 8'bz;  // Controlled_Buffer controlled_buffer_5
  assign operandB = not_5_out ? jumpPointer[7:0] : 8'bz;  // Controlled_Buffer controlled_buffer_6
  assign operandB = not_6_out ? jumpPointer[15:8] : 8'bz;  // Controlled_Buffer controlled_buffer_7
  nor nor_2 (nor_2_out, buffer_3_out, not_12_out);
  nor nor_3 (inputReady, nor_2_out, reset, nor_4_out);
  nor nor_4 (nor_4_out, inputReady, nor_5_out);
  nor nor_5 (nor_5_out, buffer_6_out, not_13_out);

  // Notes on the sheet:
  //   A
  //   SPL
  //   SPH
  //   LO
  //   HI
  //   D
  //   hier schon 74138 ?
  //   555 timer
  //   RAM
  //   IN
  //   SPL
  //   SPH
  //   FR
  //   D
  //   LO
  //   HI
  //   monostable multivibrator
  //   74240 nutzen
  //   nor_3 drives only 0 and floats otherwise
endmodule

module synced_RAM (
  input  [7:0] busIN,
  input  [12:0] adress,
  input  writeEnable,
  input  clock,
  input  outputEnable,
  output [7:0] busOUT
);

  wire buffer_1_out, buffer_2_out, buffer_3_out, buffer_4_out, buffer_5_out, buffer_6_out, buffer_7_out,
       buffer_8_out, buffer_9_out, buffer_10_out, buffer_11_out, buffer_12_out, nand_1_out, nand_2_out,
       nand_3_out, not_1_out, not_2_out, not_3_out, or_1_out, or_2_out;
  wire [7:0] ram_1_data;

  nand nand_1 (nand_1_out, writeEnable, clock);
  buf buffer_1 (buffer_1_out, nand_1_out);
  buf buffer_2 (buffer_2_out, buffer_1_out);
  buf buffer_3 (buffer_3_out, buffer_2_out);
  buf buffer_4 (buffer_4_out, buffer_3_out);
  nand nand_2 (nand_2_out, nand_1_out, outputEnable);
  buf buffer_5 (buffer_5_out, nand_2_out);
  or or_1 (or_1_out, nand_1_out, buffer_6_out);
  buf buffer_6 (buffer_6_out, buffer_4_out);
  buf buffer_7 (buffer_7_out, buffer_5_out);
  buf buffer_8 (buffer_8_out, buffer_7_out);
  buf buffer_9 (buffer_9_out, buffer_8_out);
  buf buffer_10 (buffer_10_out, buffer_9_out);
  not not_1 (not_1_out, or_1_out);
  nand nand_3 (nand_3_out, not_1_out, buffer_12_out);
  buf buffer_11 (buffer_11_out, or_1_out);
  buf buffer_12 (buffer_12_out, buffer_11_out);
  or or_2 (or_2_out, nand_2_out, buffer_10_out);
  RAM #(.addrWidth(13), .databus("bidir"), .trigger("high")) ram_1 (
    .addr(adress), .we(not_2_out), .oe(not_3_out), .data(ram_1_data));
  not not_2 (not_2_out, nand_3_out);
  not not_3 (not_3_out, or_2_out);
  _74244 u_74244_1 (
    .pin1(or_1_out), .pin2(busIN[4]), .pin3(ram_1_data[3]), .pin4(busIN[5]), .pin5(ram_1_data[2]),
    .pin6(busIN[6]), .pin7(ram_1_data[1]), .pin8(busIN[7]), .pin9(ram_1_data[0]), .pin19(or_1_out),
    .pin18(ram_1_data[4]), .pin17(busIN[3]), .pin16(ram_1_data[5]), .pin15(busIN[2]), .pin14(ram_1_data[6]),
    .pin13(busIN[1]), .pin12(ram_1_data[7]), .pin11(busIN[0]));
  _74244 u_74244_2 (
    .pin1(or_2_out), .pin2(ram_1_data[4]), .pin3(busOUT[3]), .pin4(ram_1_data[5]), .pin5(busOUT[2]),
    .pin6(ram_1_data[6]), .pin7(busOUT[1]), .pin8(ram_1_data[7]), .pin9(busOUT[0]), .pin19(or_2_out),
    .pin18(busOUT[4]), .pin17(ram_1_data[3]), .pin16(busOUT[5]), .pin15(ram_1_data[2]), .pin14(busOUT[6]),
    .pin13(ram_1_data[1]), .pin12(busOUT[7]), .pin11(ram_1_data[0]));

  // Notes on the sheet:
  //   undefined behaviour while we & oe = 1
  //   enable signals change after clock falling edge
  //   ce2 must be low during all adress transistions
  //   if we = low: adress could change
  //   20ns min diff irl
  //   edge detection
  //   data to save in ram
  //   AS7C164A
  //   read data out of ram
endmodule

module serialise_8 (
  input  clock,
  input  start,
  input  [7:0] data,
  output outputReady,
  output tick,
  output serial
);

  wire n74161_1_pin3, n74161_1_pin7, n74161_1_pin11, n74161_1_pin12, n74161_1_pin13, n74161_1_pin14,
       n74161_1_pin15, n74165_1_pin7, n74165_1_pin10, nor_1_out, not_1_out, not_2_out;

  not not_1 (not_1_out, start);
  not not_2 (not_2_out, clock);
  _74165 u_74165_1 (
    .pin1(not_1_out), .pin2(not_2_out), .pin3(data[4]), .pin4(data[5]), .pin5(data[6]), .pin6(data[7]),
    .pin7(n74165_1_pin7), .pin15(outputReady), .pin14(data[3]), .pin13(data[2]), .pin12(data[1]),
    .pin11(data[0]), .pin10(n74165_1_pin10), .pin9(serial));
  // NoConnect on n74165_1_pin7
  nor nor_1 (nor_1_out, clock, outputReady);
  _74161 u_74161_1 (
    .pin1(not_1_out), .pin2(nor_1_out), .pin3(n74161_1_pin3), .pin4(n74161_1_pin3), .pin5(n74161_1_pin3),
    .pin6(n74161_1_pin3), .pin7(n74161_1_pin7), .pin15(n74161_1_pin15), .pin14(n74161_1_pin14),
    .pin13(n74161_1_pin13), .pin12(n74161_1_pin12), .pin11(n74161_1_pin11), .pin10(n74161_1_pin7),
    .pin9(n74161_1_pin7));
  nor nor_2 (tick, outputReady, nor_1_out);
  // NoConnect on n74161_1_pin15
  // NoConnect on n74161_1_pin11
  and and_1 (outputReady, n74161_1_pin12, n74161_1_pin13, n74161_1_pin14);
  // also tied to GND on the sheet: {n74165_1_pin10, n74161_1_pin3}
  // also tied to VCC on the sheet: n74161_1_pin7

  // Notes on the sheet:
  //   read on rising edge
  //   change on falling edge
  //   8th fe high
endmodule

module deserialise_8 (
  input  serial,
  input  clock,
  input  reset,
  output [7:0] data,
  output fb
);

  wire n74161_1_pin11, n74161_1_pin12, n74161_1_pin13, n74161_1_pin14, n74161_1_pin15, n74164_1_pin3,
       n74164_1_pin4, n74164_1_pin5, n74164_1_pin6, n74164_1_pin10, n74164_1_pin11, n74164_1_pin12,
       n74164_1_pin13, n74377_1_pin1, n74377_1_pin11, nor_1_out, nor_2_out, not_1_out, not_2_out,
       pull_resistor_1_node, pull_resistor_2_node, pull_resistor_3_node;

  not not_1 (not_1_out, n74161_1_pin11);
  Pull_Resistor #(.pull(1)) pull_resistor_1 (.node(pull_resistor_1_node));
  nor nor_1 (nor_1_out, reset, nor_2_out);
  nor nor_2 (nor_2_out, clock, not_1_out);
  Pull_Resistor pull_resistor_2 (.node(pull_resistor_2_node));
  Pull_Resistor #(.pull(1)) pull_resistor_3 (.node(pull_resistor_3_node));
  _74164 u_74164_1 (
    .pin1(pull_resistor_1_node), .pin2(serial), .pin3(n74164_1_pin3), .pin4(n74164_1_pin4),
    .pin5(n74164_1_pin5), .pin6(n74164_1_pin6), .pin13(n74164_1_pin13), .pin12(n74164_1_pin12),
    .pin11(n74164_1_pin11), .pin10(n74164_1_pin10), .pin9(pull_resistor_1_node), .pin8(clock));
  not not_2 (not_2_out, clock);
  _74161 u_74161_1 (
    .pin1(nor_1_out), .pin2(not_2_out), .pin3(pull_resistor_2_node), .pin4(pull_resistor_2_node),
    .pin5(pull_resistor_2_node), .pin6(pull_resistor_2_node), .pin7(pull_resistor_3_node),
    .pin15(n74161_1_pin15), .pin14(n74161_1_pin14), .pin13(n74161_1_pin13), .pin12(n74161_1_pin12),
    .pin11(n74161_1_pin11), .pin10(pull_resistor_3_node), .pin9(pull_resistor_3_node));
  // NoConnect on n74161_1_pin15
  nor nor_3 (fb, n74161_1_pin14, n74161_1_pin13, n74161_1_pin12);
  _74377 u_74377_1 (
    .pin1(n74377_1_pin1), .pin2(data[0]), .pin3(n74164_1_pin13), .pin4(n74164_1_pin12), .pin5(data[1]),
    .pin6(data[2]), .pin7(n74164_1_pin11), .pin8(n74164_1_pin10), .pin9(data[3]), .pin19(data[4]),
    .pin18(n74164_1_pin3), .pin17(n74164_1_pin4), .pin16(data[5]), .pin15(data[6]), .pin14(n74164_1_pin5),
    .pin13(n74164_1_pin6), .pin12(data[7]), .pin11(n74377_1_pin11));
  Pull_Resistor pull_resistor_4 (.node(n74377_1_pin1));
  not not_3 (n74377_1_pin11, n74161_1_pin11);

  // Notes on the sheet:
  //   8th fe: 1 / 1st fe: 0
  //   8th falling edge
endmodule

module deserialise_16 (
  input  serial,
  input  clock,
  input  reset,
  output [15:0] data,
  output fb
);

  wire n74161_1_pin2, n74161_1_pin11, n74161_1_pin12, n74161_1_pin13, n74161_1_pin14, n74161_1_pin15,
       n74164_1_pin9, n74377_1_pin3, n74377_1_pin4, n74377_1_pin7, n74377_1_pin8, n74377_1_pin11,
       n74377_1_pin13, n74377_1_pin14, n74377_1_pin17, n74377_1_pin18, n74377_2_pin3, n74377_2_pin4,
       n74377_2_pin7, n74377_2_pin8, n74377_2_pin13, n74377_2_pin14, n74377_2_pin17, n74377_2_pin18,
       pull_resistor_1_node, pull_resistor_2_node, pull_resistor_3_node, pull_resistor_4_node,
       pull_resistor_5_node;

  Pull_Resistor pull_resistor_1 (.node(pull_resistor_1_node));
  Pull_Resistor #(.pull(1)) pull_resistor_2 (.node(pull_resistor_2_node));
  _74377 u_74377_1 (
    .pin1(pull_resistor_1_node), .pin2(data[0]), .pin3(n74377_1_pin3), .pin4(n74377_1_pin4), .pin5(data[1]),
    .pin6(data[2]), .pin7(n74377_1_pin7), .pin8(n74377_1_pin8), .pin9(data[3]), .pin19(data[7]),
    .pin18(n74377_1_pin18), .pin17(n74377_1_pin17), .pin16(data[6]), .pin15(data[5]), .pin14(n74377_1_pin14),
    .pin13(n74377_1_pin13), .pin12(data[4]), .pin11(n74377_1_pin11));
  _74164 u_74164_1 (
    .pin1(pull_resistor_2_node), .pin2(serial), .pin3(n74377_1_pin3), .pin4(n74377_1_pin4),
    .pin5(n74377_1_pin7), .pin6(n74377_1_pin8), .pin13(n74377_1_pin18), .pin12(n74377_1_pin17),
    .pin11(n74377_1_pin14), .pin10(n74377_1_pin13), .pin9(n74164_1_pin9), .pin8(clock));
  not not_1 (n74164_1_pin9, reset);
  Pull_Resistor pull_resistor_3 (.node(pull_resistor_3_node));
  Pull_Resistor #(.pull(1)) pull_resistor_4 (.node(pull_resistor_4_node));
  Pull_Resistor pull_resistor_5 (.node(pull_resistor_5_node));
  _74161 u_74161_1 (
    .pin1(n74164_1_pin9), .pin2(n74161_1_pin2), .pin3(pull_resistor_3_node), .pin4(pull_resistor_3_node),
    .pin5(pull_resistor_3_node), .pin6(pull_resistor_3_node), .pin7(pull_resistor_4_node),
    .pin15(n74161_1_pin15), .pin14(n74161_1_pin14), .pin13(n74161_1_pin13), .pin12(n74161_1_pin12),
    .pin11(n74161_1_pin11), .pin10(pull_resistor_4_node), .pin9(pull_resistor_4_node));
  not not_2 (n74161_1_pin2, clock);
  _74377 u_74377_2 (
    .pin1(pull_resistor_5_node), .pin2(data[8]), .pin3(n74377_2_pin3), .pin4(n74377_2_pin4), .pin5(data[9]),
    .pin6(data[10]), .pin7(n74377_2_pin7), .pin8(n74377_2_pin8), .pin9(data[11]), .pin19(data[15]),
    .pin18(n74377_2_pin18), .pin17(n74377_2_pin17), .pin16(data[14]), .pin15(data[13]),
    .pin14(n74377_2_pin14), .pin13(n74377_2_pin13), .pin12(data[12]), .pin11(n74377_1_pin11));
  _74164 u_74164_2 (
    .pin1(pull_resistor_2_node), .pin2(n74377_1_pin18), .pin3(n74377_2_pin3), .pin4(n74377_2_pin4),
    .pin5(n74377_2_pin7), .pin6(n74377_2_pin8), .pin13(n74377_2_pin18), .pin12(n74377_2_pin17),
    .pin11(n74377_2_pin14), .pin10(n74377_2_pin13), .pin9(n74164_1_pin9), .pin8(clock));
  not not_3 (n74377_1_pin11, n74161_1_pin15);
  nor nor_1 (fb, n74161_1_pin14, n74161_1_pin13, n74161_1_pin12, n74161_1_pin11);

  // Notes on the sheet:
  //   2nd input bit
  //   not not-enable
  //   16th falling edge
  //   high after reset
  //   16th falling edge update
endmodule

module MatrixController_16p (
  input  serial,
  input  clock,
  input  reset,
  output [15:0] anode,
  output [15:0] kathode
);

  wire deserialise_16_1_fb, n74138_1_pin7, n74138_1_pin9, n74138_1_pin10, n74138_1_pin11, n74138_1_pin12,
       n74138_1_pin13, n74138_1_pin14, n74138_1_pin15, n74138_2_pin7, n74138_2_pin9, n74138_2_pin10,
       n74138_2_pin11, n74138_2_pin12, n74138_2_pin13, n74138_2_pin14, n74138_2_pin15, n74161_1_pin3,
       n74161_1_pin7, n74161_1_pin11, n74161_1_pin12, n74161_1_pin13, n74161_1_pin14, n74161_1_pin15,
       not_1_out, pull_resistor_3_node, pull_resistor_4_node;

  not not_1 (not_1_out, reset);
  deserialise_16 deserialise_16_1 (
    .serial(serial), .clock(clock), .reset(reset), .fb(deserialise_16_1_fb), .data(anode));
  _74161 u_74161_1 (
    .pin1(not_1_out), .pin2(deserialise_16_1_fb), .pin3(n74161_1_pin3), .pin4(n74161_1_pin3),
    .pin5(n74161_1_pin3), .pin6(n74161_1_pin3), .pin7(n74161_1_pin7), .pin15(n74161_1_pin15),
    .pin14(n74161_1_pin14), .pin13(n74161_1_pin13), .pin12(n74161_1_pin12), .pin11(n74161_1_pin11),
    .pin10(n74161_1_pin7), .pin9(n74161_1_pin7));
  Pull_Resistor pull_resistor_1 (.node(n74161_1_pin3));
  Pull_Resistor #(.pull(1)) pull_resistor_2 (.node(n74161_1_pin7));
  // NoConnect on n74161_1_pin15
  Pull_Resistor #(.pull(1)) pull_resistor_3 (.node(pull_resistor_3_node));
  Pull_Resistor pull_resistor_4 (.node(pull_resistor_4_node));
  _74138 u_74138_1 (
    .pin1(n74161_1_pin14), .pin2(n74161_1_pin13), .pin3(n74161_1_pin12), .pin4(n74161_1_pin11),
    .pin5(n74161_1_pin11), .pin6(pull_resistor_3_node), .pin7(n74138_1_pin7), .pin15(n74138_1_pin15),
    .pin14(n74138_1_pin14), .pin13(n74138_1_pin13), .pin12(n74138_1_pin12), .pin11(n74138_1_pin11),
    .pin10(n74138_1_pin10), .pin9(n74138_1_pin9));
  _74138 u_74138_2 (
    .pin1(n74161_1_pin14), .pin2(n74161_1_pin13), .pin3(n74161_1_pin12), .pin4(pull_resistor_4_node),
    .pin5(pull_resistor_4_node), .pin6(n74161_1_pin11), .pin7(n74138_2_pin7), .pin15(n74138_2_pin15),
    .pin14(n74138_2_pin14), .pin13(n74138_2_pin13), .pin12(n74138_2_pin12), .pin11(n74138_2_pin11),
    .pin10(n74138_2_pin10), .pin9(n74138_2_pin9));
  not not_2 (kathode[0], n74138_1_pin15);
  not not_3 (kathode[15], n74138_1_pin14);
  not not_4 (kathode[13], n74138_1_pin13);
  not not_5 (kathode[11], n74138_1_pin12);
  not not_6 (kathode[9], n74138_1_pin11);
  not not_7 (kathode[7], n74138_1_pin10);
  not not_8 (kathode[5], n74138_1_pin9);
  not not_9 (kathode[3], n74138_1_pin7);
  not not_10 (kathode[1], n74138_2_pin15);
  not not_11 (kathode[14], n74138_2_pin14);
  not not_12 (kathode[12], n74138_2_pin13);
  not not_13 (kathode[10], n74138_2_pin12);
  not not_14 (kathode[8], n74138_2_pin11);
  not not_15 (kathode[6], n74138_2_pin10);
  not not_16 (kathode[4], n74138_2_pin9);
  not not_17 (kathode[2], n74138_2_pin7);

  // Notes on the sheet:
  //   columns / spalten
  //   row / zeile
  //   wegen interlacing auf pins achten
  //   0 after reset
  //   16th falling edge update
endmodule

module KeyboardDriver (
  input  clockIN,
  input  [7:0] keys,
  input  ready,
  output serial,
  output clock,
  output sync
);

  wire buffer_1_out, buffer_2_out, buffer_3_out, xor_1_out, xor_2_out, xor_3_out, xor_4_out, xor_5_out,
       xor_6_out, xor_7_out, xor_8_out;

  xor xor_1 (xor_1_out, keys[0], keys[1]);
  xor xor_2 (xor_2_out, xor_1_out, keys[2]);
  xor xor_3 (xor_3_out, xor_2_out, keys[3]);
  xor xor_4 (xor_4_out, xor_3_out, keys[4]);
  xor xor_5 (xor_5_out, xor_4_out, keys[5]);
  xor xor_6 (xor_6_out, xor_5_out, keys[6]);
  buf buffer_1 (buffer_1_out, xor_7_out);
  buf buffer_2 (buffer_2_out, buffer_1_out);
  xor xor_7 (xor_7_out, xor_6_out, keys[7]);
  buf buffer_3 (buffer_3_out, buffer_2_out);
  xor xor_8 (xor_8_out, buffer_3_out, xor_7_out);
  and and_1 (sync, ready, xor_8_out);
  serialise_8 serialise_8_1 (
    .clock(clockIN), .start(sync), .data(keys), .serial(serial), .tick(clock));  // open: outputReady

  // Notes on the sheet:
  //   edge detector
endmodule

module hw_timer (
  input  reset,
  input  tick,
  input  active,
  input  switch,
  output [7:0] timestamp
);

  wire n74161_1_pin3, n74161_1_pin7, n74161_1_pin11, n74161_1_pin12, n74161_1_pin13, n74161_1_pin14,
       n74161_1_pin15, n74161_2_pin3, n74161_2_pin7, n74161_2_pin11, n74161_2_pin12, n74161_2_pin13,
       n74161_2_pin14, n74161_2_pin15, n74161_3_pin3, n74161_3_pin7, n74161_3_pin11, n74161_3_pin12,
       n74161_3_pin13, n74161_3_pin14, n74161_3_pin15, n74161_4_pin3, n74161_4_pin7, n74161_4_pin11,
       n74161_4_pin12, n74161_4_pin13, n74161_4_pin14, n74161_4_pin15, nand_1_out, nand_2_out, not_1_out,
       not_2_out, not_3_out, not_4_out, not_5_out;

  not not_1 (not_1_out, reset);
  not not_2 (not_2_out, switch);
  _74161 u_74161_1 (
    .pin1(not_1_out), .pin2(tick), .pin3(n74161_1_pin3), .pin4(n74161_1_pin3), .pin5(n74161_1_pin3),
    .pin6(n74161_1_pin3), .pin7(n74161_1_pin7), .pin15(n74161_1_pin15), .pin14(n74161_1_pin14),
    .pin13(n74161_1_pin13), .pin12(n74161_1_pin12), .pin11(n74161_1_pin11), .pin10(n74161_1_pin7),
    .pin9(n74161_1_pin7));
  nand nand_1 (nand_1_out, active, switch);
  nand nand_2 (nand_2_out, active, not_2_out);
  not not_3 (not_3_out, n74161_1_pin15);
  _74161 u_74161_2 (
    .pin1(not_1_out), .pin2(not_3_out), .pin3(n74161_2_pin3), .pin4(n74161_2_pin3), .pin5(n74161_2_pin3),
    .pin6(n74161_2_pin3), .pin7(n74161_2_pin7), .pin15(n74161_2_pin15), .pin14(n74161_2_pin14),
    .pin13(n74161_2_pin13), .pin12(n74161_2_pin12), .pin11(n74161_2_pin11), .pin10(n74161_2_pin7),
    .pin9(n74161_2_pin7));
  _74244 u_74244_1 (
    .pin1(nand_2_out), .pin2(n74161_1_pin14), .pin3(timestamp[0]), .pin4(n74161_1_pin13),
    .pin5(timestamp[1]), .pin6(n74161_1_pin12), .pin7(timestamp[2]), .pin8(n74161_1_pin11),
    .pin9(timestamp[3]), .pin19(nand_2_out), .pin18(timestamp[7]), .pin17(n74161_2_pin11),
    .pin16(timestamp[6]), .pin15(n74161_2_pin12), .pin14(timestamp[5]), .pin13(n74161_2_pin13),
    .pin12(timestamp[4]), .pin11(n74161_2_pin14));
  not not_4 (not_4_out, n74161_2_pin15);
  _74161 u_74161_3 (
    .pin1(not_1_out), .pin2(not_4_out), .pin3(n74161_3_pin3), .pin4(n74161_3_pin3), .pin5(n74161_3_pin3),
    .pin6(n74161_3_pin3), .pin7(n74161_3_pin7), .pin15(n74161_3_pin15), .pin14(n74161_3_pin14),
    .pin13(n74161_3_pin13), .pin12(n74161_3_pin12), .pin11(n74161_3_pin11), .pin10(n74161_3_pin7),
    .pin9(n74161_3_pin7));
  Pull_Resistor pull_resistor_1 (.node(timestamp));
  not not_5 (not_5_out, n74161_3_pin15);
  _74161 u_74161_4 (
    .pin1(not_1_out), .pin2(not_5_out), .pin3(n74161_4_pin3), .pin4(n74161_4_pin3), .pin5(n74161_4_pin3),
    .pin6(n74161_4_pin3), .pin7(n74161_4_pin7), .pin15(n74161_4_pin15), .pin14(n74161_4_pin14),
    .pin13(n74161_4_pin13), .pin12(n74161_4_pin12), .pin11(n74161_4_pin11), .pin10(n74161_4_pin7),
    .pin9(n74161_4_pin7));
  // NoConnect on n74161_4_pin15
  _74244 u_74244_2 (
    .pin1(nand_1_out), .pin2(n74161_3_pin14), .pin3(timestamp[7]), .pin4(n74161_3_pin13),
    .pin5(timestamp[6]), .pin6(n74161_3_pin12), .pin7(timestamp[5]), .pin8(n74161_3_pin11),
    .pin9(timestamp[4]), .pin19(nand_1_out), .pin18(timestamp[0]), .pin17(n74161_4_pin11),
    .pin16(timestamp[1]), .pin15(n74161_4_pin12), .pin14(timestamp[2]), .pin13(n74161_4_pin13),
    .pin12(timestamp[3]), .pin11(n74161_4_pin14));
  // also tied to GND on the sheet: {n74161_1_pin3, n74161_2_pin3, n74161_3_pin3, n74161_4_pin3}
  // also tied to VCC on the sheet: {n74161_1_pin7, n74161_2_pin7, n74161_3_pin7, n74161_4_pin7}

  // Notes on the sheet:
  //   low byte
  //   high byte
endmodule

module overflow (
  input  sub,
  input  x,
  input  y,
  input  r,
  output out_5
);

  wire nand_1_out, not_1_out, or_1_out, xor_1_out;

  xor xor_1 (xor_1_out, sub, x);
  not not_1 (not_1_out, r);
  or or_1 (or_1_out, xor_1_out, y, not_1_out);
  nand nand_1 (nand_1_out, y, xor_1_out, not_1_out);
  nand nand_2 (out_5, or_1_out, nand_1_out);
endmodule

module ic_tests (
  input  in_1,
  input  in_2,
  input  in_3,
  input  in_4,
  input  in_5,
  input  in_6,
  input  clk,
  input  in_8,
  input  [7:0] in_9,
  input  [7:0] in_10,
  input  in_11,
  input  in_12,
  input  btn,
  input  in_14,
  input  in_15,
  input  in_16,
  input  in_17,
  input  in_18
);

  wire and_1_out, and_2_out, and_3_out, and_4_out, and_5_out, and_6_out, and_7_out, and_8_out, and_9_out,
       buffer_1_out, buffer_2_out, buffer_3_out, buffer_4_out, buffer_5_out, buffer_6_out,
       matrixcontroller_16p_1_p4, matrixcontroller_16p_1_p5, n7402_1_pin2, n7402_1_pin3, n7402_1_pin5,
       n7402_1_pin6, n7402_1_pin8, n7402_1_pin9, n7402_1_pin11, n7402_1_pin12, n7402_2_pin2, n7402_2_pin3,
       n7402_2_pin5, n7402_2_pin6, n7402_2_pin8, n7402_2_pin9, n7402_2_pin11, n7402_2_pin12, n74138_1_pin7,
       n74138_1_pin9, n74138_1_pin10, n74138_1_pin11, n74138_1_pin12, n74138_1_pin13, n74138_1_pin14,
       n74138_1_pin15, n74138_2_pin7, n74138_2_pin9, n74138_2_pin10, n74138_2_pin11, n74138_2_pin12,
       n74138_2_pin13, n74138_2_pin14, n74138_2_pin15, n74161_1_pin3, n74161_1_pin7, n74161_1_pin11,
       n74161_1_pin12, n74161_1_pin13, n74161_1_pin14, n74161_1_pin15, n74240_1_pin3, n74240_1_pin5,
       n74240_1_pin7, n74240_1_pin9, n74240_1_pin12, n74240_1_pin14, n74240_1_pin16, n74240_1_pin18,
       n74240_2_pin1, n74240_2_pin2, n74240_2_pin3, n74240_2_pin4, n74240_2_pin5, n74240_2_pin6,
       n74240_2_pin7, n74240_2_pin8, n74240_2_pin9, n74240_2_pin11, n74240_2_pin12, n74240_2_pin13,
       n74240_2_pin14, n74240_2_pin15, n74240_2_pin16, n74240_2_pin17, n74240_2_pin18, n74244_1_pin3,
       n74244_1_pin5, n74244_1_pin7, n74244_1_pin9, n74244_1_pin12, n74244_1_pin14, n74244_1_pin16,
       n74244_1_pin18, n74377_1_pin11, n74377_2_pin2, n74377_2_pin5, n74377_2_pin6, n74377_2_pin9,
       n74377_2_pin14, n74377_2_pin17, n74377_2_pin18, n74377_2_pin19, nand_1_out, not_1_out, not_2_out,
       not_3_out, not_4_out, not_5_out, not_6_out, not_7_out, not_8_out, not_9_out, not_10_out, not_11_out,
       not_12_out, not_13_out, not_14_out, not_15_out, not_16_out, not_17_out, not_18_out, not_19_out,
       not_20_out, not_21_out, not_22_out, not_23_out, not_24_out, not_25_out, not_26_out, not_27_out,
       or_1_out, or_2_out, or_3_out, or_4_out, or_5_out, or_6_out, or_7_out, or_8_out, or_9_out,
       pull_resistor_1_node, pull_resistor_2_node, pull_resistor_3_node, undriven, undriven_2;
  wire [7:0] n74377_1_pin9;

  not not_1 (not_1_out, undriven);
  _74377 u_74377_1 (
    .pin1(not_1_out), .pin2(n74377_1_pin9[5]), .pin3(in_9[4]), .pin4(in_9[5]), .pin5(n74377_1_pin9[6]),
    .pin6(n74377_1_pin9[7]), .pin7(in_9[6]), .pin8(in_9[7]), .pin9(n74377_1_pin9[0]),
    .pin19(n74377_1_pin9[4]), .pin18(in_9[3]), .pin17(in_9[2]), .pin16(n74377_1_pin9[3]),
    .pin15(n74377_1_pin9[2]), .pin14(in_9[1]), .pin13(in_9[0]), .pin12(n74377_1_pin9[1]),
    .pin11(n74377_1_pin11));
  and and_1 (and_1_out, in_17, in_18);
  not not_2 (not_2_out, in_17);
  or or_1 (or_1_out, not_2_out, not_3_out);
  not not_3 (not_3_out, in_18);
  and and_2 (and_2_out, in_17, not_4_out);
  not not_4 (not_4_out, in_18);
  not not_5 (not_5_out, in_17);
  or or_2 (or_2_out, not_5_out, in_18);
  not not_6 (not_6_out, or_1_out);
  not not_7 (not_7_out, or_2_out);
  and and_3 (and_3_out, in_17, in_18);
  not not_8 (not_8_out, in_17);
  or or_3 (or_3_out, not_8_out, not_9_out);
  not not_9 (not_9_out, in_18);
  and and_4 (and_4_out, in_17, not_10_out);
  not not_10 (not_10_out, in_18);
  not not_11 (not_11_out, in_17);
  or or_4 (or_4_out, not_11_out, in_18);
  _74161 u_74161_1 (
    .pin1(in_5), .pin2(in_6), .pin3(n74161_1_pin3), .pin4(n74161_1_pin3), .pin5(n74161_1_pin3),
    .pin6(n74161_1_pin3), .pin7(n74161_1_pin7), .pin15(n74161_1_pin15), .pin14(n74161_1_pin14),
    .pin13(n74161_1_pin13), .pin12(n74161_1_pin12), .pin11(n74161_1_pin11), .pin10(n74161_1_pin7),
    .pin9(n74161_1_pin7));
  // NoConnect on n74161_1_pin15
  not not_12 (not_12_out, and_3_out);
  not not_13 (not_13_out, and_4_out);
  not not_14 (not_14_out, in_17);
  and and_5 (and_5_out, not_14_out, not_15_out);
  not not_15 (not_15_out, in_18);
  or or_5 (or_5_out, in_17, in_18);
  not not_16 (not_16_out, in_17);
  and and_6 (and_6_out, not_16_out, in_18);
  or or_6 (or_6_out, in_17, not_17_out);
  not not_17 (not_17_out, in_18);
  _74240 u_74240_1 (
    .pin1(in_12), .pin2(in_10[4]), .pin3(n74240_1_pin3), .pin4(in_10[5]), .pin5(n74240_1_pin5),
    .pin6(in_10[6]), .pin7(n74240_1_pin7), .pin8(in_10[7]), .pin9(n74240_1_pin9), .pin19(in_12),
    .pin18(n74240_1_pin18), .pin17(in_10[3]), .pin16(n74240_1_pin16), .pin15(in_10[2]),
    .pin14(n74240_1_pin14), .pin13(in_10[1]), .pin12(n74240_1_pin12), .pin11(in_10[0]));
  not not_18 (not_18_out, and_5_out);
  not not_19 (not_19_out, and_6_out);
  not not_20 (not_20_out, in_17);
  and and_7 (and_7_out, not_20_out, not_21_out);
  not not_21 (not_21_out, in_18);
  or or_7 (or_7_out, in_17, in_18);
  not not_22 (not_22_out, in_17);
  and and_8 (and_8_out, not_22_out, in_18);
  or or_8 (or_8_out, in_17, not_23_out);
  not not_23 (not_23_out, in_18);
  not not_24 (not_24_out, or_7_out);
  not not_25 (not_25_out, or_8_out);
  _74244 u_74244_1 (
    .pin1(in_12), .pin2(in_10[4]), .pin3(n74244_1_pin3), .pin4(in_10[5]), .pin5(n74244_1_pin5),
    .pin6(in_10[6]), .pin7(n74244_1_pin7), .pin8(in_10[7]), .pin9(n74244_1_pin9), .pin19(in_12),
    .pin18(n74244_1_pin18), .pin17(in_10[3]), .pin16(n74244_1_pin16), .pin15(in_10[2]),
    .pin14(n74244_1_pin14), .pin13(in_10[1]), .pin12(n74244_1_pin12), .pin11(in_10[0]));
  Pull_Resistor #(.pull(1)) pull_resistor_1 (.node(pull_resistor_1_node));
  Pull_Resistor pull_resistor_2 (.node(pull_resistor_2_node));
  _74138 u_74138_1 (
    .pin1(in_1), .pin2(in_2), .pin3(in_3), .pin4(in_4), .pin5(in_4), .pin6(pull_resistor_1_node),
    .pin7(n74138_1_pin7), .pin15(n74138_1_pin15), .pin14(n74138_1_pin14), .pin13(n74138_1_pin13),
    .pin12(n74138_1_pin12), .pin11(n74138_1_pin11), .pin10(n74138_1_pin10), .pin9(n74138_1_pin9));
  _74138 u_74138_2 (
    .pin1(in_1), .pin2(in_2), .pin3(in_3), .pin4(pull_resistor_2_node), .pin5(pull_resistor_2_node),
    .pin6(in_4), .pin7(n74138_2_pin7), .pin15(n74138_2_pin15), .pin14(n74138_2_pin14),
    .pin13(n74138_2_pin13), .pin12(n74138_2_pin12), .pin11(n74138_2_pin11), .pin10(n74138_2_pin10),
    .pin9(n74138_2_pin9));
  _74240 u_74240_2 (
    .pin1(n74240_2_pin1), .pin2(n74240_2_pin2), .pin3(n74240_2_pin3), .pin4(n74240_2_pin4),
    .pin5(n74240_2_pin5), .pin6(n74240_2_pin6), .pin7(n74240_2_pin7), .pin8(n74240_2_pin8),
    .pin9(n74240_2_pin9), .pin19(n74240_2_pin1), .pin18(n74240_2_pin18), .pin17(n74240_2_pin17),
    .pin16(n74240_2_pin16), .pin15(n74240_2_pin15), .pin14(n74240_2_pin14), .pin13(n74240_2_pin13),
    .pin12(n74240_2_pin12), .pin11(n74240_2_pin11));
  _7402 u_7402_1 (
    .pin1(n74240_2_pin2), .pin2(n7402_1_pin2), .pin3(n7402_1_pin3), .pin4(n74240_2_pin4),
    .pin5(n7402_1_pin5), .pin6(n7402_1_pin6), .pin13(n74240_2_pin17), .pin12(n7402_1_pin12),
    .pin11(n7402_1_pin11), .pin10(n74240_2_pin15), .pin9(n7402_1_pin9), .pin8(n7402_1_pin8));
  _7402 u_7402_2 (
    .pin1(n74240_2_pin6), .pin2(n7402_2_pin2), .pin3(n7402_2_pin3), .pin4(n74240_2_pin8),
    .pin5(n7402_2_pin5), .pin6(n7402_2_pin6), .pin13(n74240_2_pin13), .pin12(n7402_2_pin12),
    .pin11(n7402_2_pin11), .pin10(n74240_2_pin11), .pin9(n7402_2_pin9), .pin8(n7402_2_pin8));
  Pull_Resistor pull_resistor_3 (.node(pull_resistor_3_node));
  // MatrixController_16p matrixcontroller_16p_1: pin names not known; wires that end beside it: in_14, in_15, in_16, matrixcontroller_16p_1_p4, matrixcontroller_16p_1_p5
  _74377 u_74377_2 (
    .pin1(pull_resistor_3_node), .pin2(n74377_2_pin2), .pin3(in_8), .pin4(n74377_2_pin2),
    .pin5(n74377_2_pin5), .pin6(n74377_2_pin6), .pin7(n74377_2_pin5), .pin8(n74377_2_pin6),
    .pin9(n74377_2_pin9), .pin19(n74377_2_pin19), .pin18(n74377_2_pin18), .pin17(n74377_2_pin17),
    .pin16(n74377_2_pin18), .pin15(n74377_2_pin17), .pin14(n74377_2_pin14), .pin13(n74377_2_pin9),
    .pin12(n74377_2_pin14), .pin11(in_11));
  // DotMatrix #(.dotshape("circle"), .inputtype("select"), .matrixcols(16), .matrixrows(16)) dotmatrix_1: pin names not known; wires that end beside it: matrixcontroller_16p_1_p4, matrixcontroller_16p_1_p5, n74377_2_pin2, n74377_2_pin5, n74377_2_pin6, n74377_2_pin9, n74377_2_pin14, n74377_2_pin17, n74377_2_pin18, n74377_2_pin19
  not not_26 (not_26_out, undriven_2);
  buf buffer_1 (buffer_1_out, undriven_2);
  buf buffer_2 (buffer_2_out, buffer_1_out);
  buf buffer_3 (buffer_3_out, buffer_2_out);
  nand nand_1 (nand_1_out, not_26_out, buffer_3_out);
  buf buffer_4 (buffer_4_out, btn);
  buf buffer_5 (buffer_5_out, buffer_4_out);
  buf buffer_6 (buffer_6_out, buffer_5_out);
  not not_27 (not_27_out, btn);
  or or_9 (or_9_out, clk, and_9_out);
  and and_9 (and_9_out, nand_1_out, or_9_out);
  // NOR_Gate nor_1 has open pins: in0=buffer_6_out, in1=not_27_out, out=open
  // also tied to GND on the sheet: n74161_1_pin3
  // also tied to VCC on the sheet: n74161_1_pin7

  // Notes on the sheet:
  //   74377 = Register
  //   3
  //   4
  //   4
  //   3
  //   74161 = Counter
  //   2
  //   5
  //   3
  //   4
  //   74240 = Inverter
  //   4
  //   3
  //   3
  //   4
  //   5
  //   2
  //   4
  //   3
  //   74244 = Buffer
  //   falling edge detector
  //   clock hold
endmodule
